// Logisim project s-mips.circ as structural Verilog: 62 circuits, main circuit S-MIPS Board
module S_MIPS_Board (
  input  DESHABILITAR_DISPATCHER,
  output halt
);

  wire button_1_out, CLK, CS, d_ff_1_q, LCLR, LoadRAM, LoadRAMOn, LW, R_R_W, R_W, ram_dispatcher_1_finished,
       RCS, Reset_out, RST, TTY_EN;
  wire [2:0] KDB;
  wire [3:0] LMask, Mask, ram_1_read_time, ram_1_write_time, RMask;
  wire [6:0] KDB_DATA, TTY_DATA;
  wire [15:0] Addr, LAddr, RAddr;
  wire [31:0] I0, I1, I2, I3, LData, ram_1_data_out_0, ram_1_data_out_1, ram_1_data_out_2, ram_1_data_out_3,
       RI0, RI1, RI2, RI3;

  TTY #(.rows(25), .cols(80)) tty_1 (.data(TTY_DATA), .clk(CLK), .we(TTY_EN), .clr(RST));
  not not_1 (LoadRAMOn, ram_dispatcher_1_finished);
  RAM_Dispatcher ram_dispatcher_1 (
    .WriteTime(ram_1_write_time), .Clock(CLK), .Data(LData), .Address(LAddr), .Mask(LMask),
    .Finished(ram_dispatcher_1_finished), .Write(LW), .CLR(LCLR));
  Keyboard #(.buflen(64)) keyboard_1 (.clk(CLK), .re(KDB[0]), .clr(KDB[1]), .avail(KDB[2]), .data(KDB_DATA));
  RAM ram_1 (
    .Address(RAddr), .Data_Out_0(ram_1_data_out_0), .Data_Out_1(ram_1_data_out_1),
    .Data_Out_2(ram_1_data_out_2), .Data_Out_3(ram_1_data_out_3), .Data_In_0(RI0), .Data_In_1(RI1),
    .Data_In_2(RI2), .Data_In_3(RI3), .Mask(RMask), .nRead_Write(R_R_W), .Chip_Select(RCS),
    .Read_Time(ram_1_read_time), .Reset(button_1_out), .Write_Time(ram_1_write_time));
  Button button_1 (.out(button_1_out));
  D_Flip_Flop d_ff_1 (.clk(CLK), .D(1'b1), .Q(d_ff_1_q), .reset(Reset_out));  // open: Qn, preset, en
  Button Reset (.out(Reset_out));
  S_MIPS s_mips_1 (
    .Kbd_Enable(KDB[0]), .Address(Addr), .Kbd_Clear(KDB[1]), .Kbd_Available(KDB[2]), .RAM_In_0(I0),
    .Kbd_ASCII_Data(KDB_DATA), .RAM_In_1(I1), .TTY_Enable(TTY_EN), .RAM_In_2(I2), .RAM_In_3(I3),
    .TTY_ASCII_Data(TTY_DATA), .Reset(RST), .RAM_Out_0(ram_1_data_out_0), .Clock(CLK),
    .RAM_Out_1(ram_1_data_out_1), .Stop(halt), .RAM_Out_2(ram_1_data_out_2), .RAM_Out_3(ram_1_data_out_3),
    .Mask(Mask), .Read_Time(ram_1_read_time), .Write_Time(ram_1_write_time), .nRead_Write(R_W),
    .Chip_Select(CS));
  D_Flip_Flop d_ff_2 (.clk(CLK), .D(d_ff_1_q), .Qn(LCLR), .reset(Reset_out));  // open: Q, preset, en
  or or_1 (RST, LCLR, LoadRAM);
  Clock clock_1 (.out(CLK));
  Multiplexer #(.width(32), .enable("false")) multiplexer_1 (.in0(I0), .in1(LData), .out(RI0), .sel(LoadRAM));
  Multiplexer #(.width(32), .enable("false")) multiplexer_2 (.in0(I1), .in1(LData), .out(RI1), .sel(LoadRAM));
  Multiplexer #(.width(32), .enable("false")) multiplexer_3 (.in0(I2), .in1(LData), .out(RI2), .sel(LoadRAM));
  Multiplexer #(.width(32), .enable("false")) multiplexer_4 (.in0(I3), .in1(LData), .out(RI3), .sel(LoadRAM));
  and and_1 (LoadRAM, ~DESHABILITAR_DISPATCHER, LoadRAMOn);  // AND_Gate
  Multiplexer #(.width(16), .enable("false")) multiplexer_5 (.in0(Addr), .in1(LAddr), .out(RAddr), .sel(LoadRAM));
  Multiplexer #(.width(4), .enable("false")) multiplexer_6 (.in0(Mask), .in1(LMask), .out(RMask), .sel(LoadRAM));
  Multiplexer #(.enable("false")) multiplexer_7 (.in0(CS), .in1(LW), .out(RCS), .sel(LoadRAM));
  Multiplexer #(.enable("false")) multiplexer_8 (.in0(R_W), .in1(LW), .out(R_R_W), .sel(LoadRAM));

  // Notes on the sheet:
  //   NO MODIFICAR
  //   Keyboard
endmodule

module RAM (
  input  [15:0] Address,
  input  [31:0] Data_In_0,
  input  [31:0] Data_In_1,
  input  [31:0] Data_In_2,
  input  [31:0] Data_In_3,
  input  [3:0] Mask,
  input  nRead_Write,
  input  Chip_Select,
  input  Reset,
  output [31:0] Data_Out_0,
  output [31:0] Data_Out_1,
  output [31:0] Data_Out_2,
  output [31:0] Data_Out_3,
  output [3:0] Read_Time,
  output [3:0] Write_Time
);

  wire and_2_out, and_3_out, and_4_out, and_5_out, and_6_out, and_7_out, and_8_out, and_9_out, Changed, CLK,
       comparator_2_eq, comparator_3_eq, comparator_4_eq, comparator_5_eq, comparator_6_eq, Count,
       demultiplexer_3_out0, Idle, Idle_q, Load, Load0, Load1, nand_1_out, or_1_out, or_2_out, or_3_out,
       or_4_out, or_5_out, or_6_out, or_7_out, or_8_out, or_9_out, or_10_out, Proc_q, Update_Mem, Zero_Time;
  wire [3:0] counter_1_q, multiplexer_1_out, subtractor_1_out;
  wire [31:0] register_1_q, register_2_q, register_3_q, register_4_q, register_5_q;

  // Probe on 4'b0011
  // Probe on 4'b0010
  Multiplexer #(.width(4), .enable("false")) multiplexer_1 (
    .in0(4'b0011), .in1(4'b0010), .out(multiplexer_1_out), .sel(nRead_Write));
  or or_1 (or_1_out, Idle, Update_Mem);
  or or_2 (or_2_out, ~Chip_Select, Reset);  // OR_Gate
  Subtractor #(.width(4)) subtractor_1 (.a(multiplexer_1_out), .b(4'b0010), .out(subtractor_1_out));  // open: bin, bout
  Demultiplexer #(.enable("false")) demultiplexer_1 (.out0(Idle), .out1(Load0), .in(Idle_q), .sel(Changed));
  D_Flip_Flop u_Idle (.clk(CLK), .D(or_1_out), .Q(Idle_q), .preset(or_2_out));  // open: Qn, en, reset
  // Probe on counter_1_q
  Counter #(.width(4), .max('hf)) counter_1 (
    .load(Load), .D(subtractor_1_out), .count(Count), .Q(counter_1_q), .clk(CLK), .clr(or_3_out));  // open: carry
  or or_3 (or_3_out, ~Chip_Select, Reset);  // OR_Gate
  Comparator #(.width(4), .mode("unsigned")) comparator_1 (
    .a(4'b0000), .b(counter_1_q), .eq(Zero_Time));  // open: gt, lt
  or or_4 (or_4_out, Count, Load0, Load1);
  Register #(.width(32)) register_1 (.D(Data_In_0), .en(Chip_Select), .Q(register_1_q), .clk(CLK), .clr(or_5_out));
  or or_5 (or_5_out, ~Chip_Select, Reset);  // OR_Gate
  Register #(.width(32)) register_2 (.D(Data_In_1), .en(Chip_Select), .Q(register_2_q), .clk(CLK), .clr(or_6_out));
  or or_6 (or_6_out, ~Chip_Select, Reset);  // OR_Gate
  Register #(.width(32)) register_3 (.D(Data_In_2), .en(Chip_Select), .Q(register_3_q), .clk(CLK), .clr(or_7_out));
  or or_7 (or_7_out, ~Chip_Select, Reset);  // OR_Gate
  Register #(.width(32)) register_4 (.D(Data_In_3), .en(Chip_Select), .Q(register_4_q), .clk(CLK), .clr(or_8_out));
  or or_8 (or_8_out, ~Chip_Select, Reset);  // OR_Gate
  Register #(.width(32)) register_5 (
    .D({{11{1'b1}}, nRead_Write, Mask, Address}), .en(Chip_Select), .Q(register_5_q), .clk(CLK),
    .clr(or_9_out));
  or or_9 (or_9_out, ~Chip_Select, Reset);  // OR_Gate
  D_Flip_Flop Proc (.clk(CLK), .D(or_4_out), .Q(Proc_q), .reset(or_10_out));  // open: Qn, preset, en
  or or_10 (or_10_out, ~Chip_Select, Reset);  // OR_Gate
  Demultiplexer #(.enable("false")) demultiplexer_2 (
    .out0(Count), .out1(Update_Mem), .in(demultiplexer_3_out0), .sel(Zero_Time));
  Demultiplexer #(.enable("false")) demultiplexer_3 (
    .out0(demultiplexer_3_out0), .out1(Load1), .in(Proc_q), .sel(Changed));
  Clock clock_1 (.out(CLK));
  Comparator #(.width(32)) comparator_2 (.a(register_1_q), .b(Data_In_0), .eq(comparator_2_eq));  // open: gt, lt
  Comparator #(.width(32)) comparator_3 (.a(register_2_q), .b(Data_In_1), .eq(comparator_3_eq));  // open: gt, lt
  Comparator #(.width(32)) comparator_4 (.a(register_3_q), .b(Data_In_2), .eq(comparator_4_eq));  // open: gt, lt
  Comparator #(.width(32)) comparator_5 (.a(register_4_q), .b(Data_In_3), .eq(comparator_5_eq));  // open: gt, lt
  Comparator #(.width(32)) comparator_6 (
    .a(register_5_q), .b({{11{1'b1}}, nRead_Write, Mask, Address}), .eq(comparator_6_eq));  // open: gt, lt
  nand nand_1 (nand_1_out, comparator_6_eq, comparator_2_eq, comparator_3_eq, comparator_4_eq, comparator_5_eq);
  and and_1 (Changed, nand_1_out, Chip_Select);
  or or_11 (Load, Count, Load1, Load0);
  and and_2 (and_2_out, Mask[0], Update_Mem, nRead_Write);
  and and_3 (and_3_out, Mask[1], Update_Mem, nRead_Write);
  and and_4 (and_4_out, Mask[2], Update_Mem, nRead_Write);
  and and_5 (and_5_out, Mask[3], Update_Mem, nRead_Write);
  RAM_part #(.addrWidth(16), .dataWidth(32), .bus("separate")) ram_1 (
    .addr(Address), .din(Data_In_0), .data(Data_Out_0), .str(and_2_out), .sel(Chip_Select), .clk(CLK),
    .ld(and_6_out), .clr(Reset));
  and and_6 (and_6_out, ~nRead_Write, Idle);  // AND_Gate
  RAM_part #(.addrWidth(16), .dataWidth(32), .bus("separate")) ram_2 (
    .addr(Address), .din(Data_In_1), .data(Data_Out_1), .str(and_3_out), .sel(Chip_Select), .clk(CLK),
    .ld(and_7_out), .clr(Reset));
  and and_7 (and_7_out, ~nRead_Write, Idle);  // AND_Gate
  RAM_part #(.addrWidth(16), .dataWidth(32), .bus("separate")) ram_3 (
    .addr(Address), .din(Data_In_2), .data(Data_Out_2), .str(and_4_out), .sel(Chip_Select), .clk(CLK),
    .ld(and_8_out), .clr(Reset));
  and and_8 (and_8_out, ~nRead_Write, Idle);  // AND_Gate
  RAM_part #(.addrWidth(16), .dataWidth(32), .bus("separate")) ram_4 (
    .addr(Address), .din(Data_In_3), .data(Data_Out_3), .str(and_5_out), .sel(Chip_Select), .clk(CLK),
    .ld(and_9_out), .clr(Reset));
  and and_9 (and_9_out, ~nRead_Write, Idle);  // AND_Gate

  assign Read_Time = 4'b0011;
  assign Write_Time = 4'b0010;

  // Other names for the same wires on the sheet: M0 = Mask[0]; M1 = Mask[1]; M2 = Mask[2]; M3 = Mask[3];
  //   RW = nRead_Write; CLR = Reset; CS = Chip_Select; Load2 = Count

  // Notes on the sheet:
  //   NO MODIFICAR
  //   excepto quizás los valores RT y WT
  //   BANK0
  //   BANK1
  //   BANK2
  //   BANK3
endmodule

module RAM_Dispatcher (
  input  [3:0] WriteTime,
  input  Clock,
  input  CLR,
  output [31:0] Data,
  output [15:0] Address,
  output [3:0] Mask,
  output Finished,
  output Write
);

  wire demultiplexer_2_out1, demultiplexer_3_out1, End, IDLE_q, IncAddr, Load, or_1_out, or_2_out, While_q,
       WriteEnd;
  wire [3:0] counter_1_q;
  wire [31:0] CurrentAddress_q;

  Counter #(.width(32), .max('hffffffff)) CurrentAddress (
    .count(IncAddr), .Q({CurrentAddress_q[31:18], Address, CurrentAddress_q[1:0]}), .clk(Clock), .clr(CLR));  // open: load, D, carry
  or or_1 (or_1_out, IncAddr, demultiplexer_3_out1, Finished);
  D_Flip_Flop IDLE (.clk(Clock), .D(or_1_out), .Q(IDLE_q), .preset(CLR));  // open: Qn, en, reset
  Demultiplexer #(.enable("false")) demultiplexer_1 (.out0(Load), .out1(Finished), .in(IDLE_q), .sel(End));
  D_Flip_Flop While (.clk(Clock), .D(or_2_out), .Q(While_q), .reset(CLR));  // open: Qn, preset, en
  or or_2 (or_2_out, Write, Load);
  RAM_part #(.addrWidth(18), .dataWidth(32)) ram_1 (
    .addr({Address, CurrentAddress_q[1:0]}), .data(Data), .clk(Clock));  // open: sel, ld, clr
  Demultiplexer #(.enable("false")) demultiplexer_2 (
    .out0(Write), .out1(demultiplexer_2_out1), .in(While_q), .sel(WriteEnd));
  Decoder #(.select(2)) decoder_1 (
    .out0(Mask[0]), .out1(Mask[1]), .out2(Mask[2]), .out3(Mask[3]), .sel(CurrentAddress_q[1:0]));  // open: en
  Demultiplexer #(.enable("false")) demultiplexer_3 (
    .out0(IncAddr), .out1(demultiplexer_3_out1), .in(demultiplexer_2_out1), .sel(End));
  Counter #(.width(4), .max('hf)) counter_1 (
    .load(Load), .D(WriteTime), .count(Write), .Q(counter_1_q), .clk(Clock));  // open: carry, clr
  Comparator #(.width(32)) comparator_1 (.a(Data), .b({32{1'b1}}), .eq(End));  // open: gt, lt
  Comparator #(.width(4)) comparator_2 (.a(4'b0000), .b(counter_1_q), .eq(WriteEnd));  // open: gt, lt

  // Other names for the same wires on the sheet: CLK = Clock; Count = Write; WT[3:0] = WriteTime
endmodule

module S_MIPS (
  input  Kbd_Available,
  input  [6:0] Kbd_ASCII_Data,
  input  [31:0] RAM_Out_0,
  input  [31:0] RAM_Out_1,
  input  Reset,
  input  [31:0] RAM_Out_2,
  input  Clock,
  input  [31:0] RAM_Out_3,
  input  [3:0] Read_Time,
  input  [3:0] Write_Time,
  output Kbd_Enable,
  output [15:0] Address,
  output Kbd_Clear,
  output TTY_Enable,
  output [6:0] TTY_ASCII_Data,
  output Stop,
  output [31:0] RAM_In_0,
  output [31:0] RAM_In_1,
  output [31:0] RAM_In_2,
  output [31:0] RAM_In_3,
  output [3:0] Mask,
  output nRead_Write,
  output Chip_Select
);

  wire _11op, beq, bgtz, blez, bltz, bne, CACHERESP, eq, halt, inst, j, jr, kbd, lez, LI, ltz, lw, pop, push,
       RAMOP, rnd, RUN, RWA, selectRAMDP, store, sw, toRt, tty, useCTE, ValidC, WriteDP;
  wire [1:0] sel;
  wire [3:0] aluop;
  wire [4:0] rd, rs, rt;
  wire [25:0] destino;
  wire [31:0] aluo, CACHEOUTPUT, cte, efficiencecount_1_output, fromram, hit, miss, offset, PC, rso, rto, sp,
       sp_4;

  // Probe on Clock
  // Probe on Chip_Select
  // Probe on store
  and and_1 (nRead_Write, RWA, ~inst);  // AND_Gate
  InstructionDecoder instructiondecoder_1 (
    .toalu(aluop), .cte(cte), .INST(fromram), .Write(WriteDP), .push(push), .pop(pop), .jr(jr),
    .offset(offset), .beq(beq), .bne(bne), .blez(blez), .bgtz(bgtz), .bltz(bltz), .j(j), .destino(destino),
    .LoadINstruction(LI), .clk(Clock), .RAM(RAMOP), .halt(halt), .tty(tty), .kbd(kbd), .rnd(rnd), .lw(lw),
    .sw(sw), .fromRAM(selectRAMDP), .toRAM(RWA), .Rs(rs), .Rt(rt), .Rd(rd), .useCTE(useCTE), ._11op(_11op),
    .KBD_AVAIL(Kbd_Available), .toRT(toRt), .RST(Reset));
  and and_2 (TTY_Enable, tty, RUN);
  and and_3 (Kbd_Enable, kbd, RUN);
  ControlUnit controlunit_1 (
    .rst(Reset), .halt(halt), .clk(Clock), .RAMReadT(Read_Time), .RAMWriteT(Write_Time), .RAM(RAMOP),
    .R0_W1(RWA), .CACHERESPONSE(CACHERESP), .LoadInst(LI), .RUN(RUN), .stop(Stop), .chip_select(Chip_Select),
    .INST(inst), .storecache(store), .writ(ValidC), .HITS(hit), .MISSES(miss));
  RAMInterface raminterface_1 (
    .sw(sw), .push(push), .pop(pop), .ALUO(aluo), .SP___4(sp_4), .SP(sp), .Rs(rso), .Rt(rto),
    .fromRAM1(RAM_Out_0), .fromRAM2(RAM_Out_1), .fromRAM3(RAM_Out_2), .fromRAM4(RAM_Out_3), .mask(Mask),
    .addr(Address), .toRAM(RAM_In_0), .fromRAM(fromram), .PC(PC), .INST(inst), .sel(sel),
    .CACHEOUTPUT(CACHEOUTPUT), .CACHERESPONSE(CACHERESP));
  // Probe on efficiencecount_1_output
  efficiencecount efficiencecount_1 (.clock(Clock), .stop(Stop), .Output(efficiencecount_1_output), .rst(Reset));
  // Probe on hit
  // Probe on miss
  // Probe on fromram
  DataPath datapath_1 (
    .Rs(rs), .Rt_2(rt), .Rd(rd), .clk(Clock), .cte(cte), .alusel(aluop), .memory(fromram), .Rt(toRt),
    .ram1_reg0(selectRAMDP), .cte1_register0(useCTE), .W(WriteDP), .R(Reset), .RsO(rso), .push(push),
    .pop(pop), .eq(eq), .lez(lez), .ltz(ltz), .kbd(Kbd_ASCII_Data), .tty(TTY_ASCII_Data), .ALUO(aluo),
    .RtO(rto), .SP(sp), .SP_4(sp_4), .RUN(RUN), ._11op(_11op));
  // Probe on PC
  BranchControl branchcontrol_1 (
    .RIN(rso), .clk(Clock), .R(Reset), .Output(PC), .offIN(offset), .destino(destino), .beq(beq), .bne(bne),
    .blez(blez), .bgtz(bgtz), .bltz(bltz), .j(j), .jr(jr), .eq(eq), .lez(lez), .ltz(ltz), .L_RUN(RUN));
  Cache cache_1 (
    .rst(Reset), .clk(Clock), .addr(Address), .sel(sel), .store(store), .DI0(RAM_Out_0), .DI1(RAM_Out_1),
    .DI2(RAM_Out_2), .DI3(RAM_Out_3), .CACHEOut(CACHEOUTPUT), .CACHERESPONSE(CACHERESP), .CACHEENABLE(1'b1),
    .RW(ValidC), .toRAM(RAM_In_0));

  assign Kbd_Clear = Reset;
  assign RAM_In_1 = RAM_In_0;
  assign RAM_In_2 = RAM_In_0;
  assign RAM_In_3 = RAM_In_0;

  // Other names for the same wires on the sheet: CLK = Clock; CS = Chip_Select; KBD_AVAIL = Kbd_Available;
  //   CLR = Reset; KBD_CLR = Reset; KBD_DATA[6:0] = Kbd_ASCII_Data; RAM_A[15:0] = Address; RAM_MASK[3:0] = Mask;
  //   RAM_OUTPUT_0[31:0] = RAM_Out_0; RAM_OUTPUT_1[31:0] = RAM_Out_1; RAM_OUTPUT_2[31:0] = RAM_Out_2;
  //   RAM_OUTPUT_3[31:0] = RAM_Out_3; RW = nRead_Write; RAM_INPUT_0[31:0] = RAM_In_0; RAM_INPUT_1[31:0] = RAM_In_0;
  //   RAM_INPUT_2[31:0] = RAM_In_0; RAM_INPUT_3[31:0] = RAM_In_0; toram[31:0] = RAM_In_0;
  //   TTY_DATA[6:0] = TTY_ASCII_Data

  // Notes on the sheet:
  //   RAM ADDRESS
  //   DATA FROM RAM
  //   DATA TO RAM
  //   DATA WRITE MASK
  //   RAM TIMING
  //   RAM CONTROL
  //   ENABLE CACHE
  //   KEYBOARD
  //   TTY
  //   SEQUENCING
endmodule

module ControlUnit (
  input  rst,
  input  halt,
  input  clk,
  input  [3:0] RAMReadT,
  input  [3:0] RAMWriteT,
  input  RAM,
  input  R0_W1,
  input  CACHERESPONSE,
  output INST,
  output LoadInst,
  output RUN,
  output stop,
  output [31:0] HITS,
  output chip_select,
  output writ,
  output [31:0] MISSES,
  output storecache
);

  wire a, and_6_out, and_7_out, and_8_out, and_9_out, begins, d_ff_1_q, demultiplexer_1_out0,
       demultiplexer_2_out1, demultiplexer_4_out0, demultiplexer_5_out0, DO1, DO2, \end , holdstop, insbeg,
       loadInst_t, loadRam, memwait, or_1_out, or_2_out, or_3_out, or_5_out, or_6_out, or_9_out, or_10_out,
       rum, writ_t;
  wire [3:0] timeram, timewait;

  D_Flip_Flop #(.trigger("falling")) d_ff_1 (
    .clk(clk), .D(demultiplexer_2_out1), .Q(d_ff_1_q), .preset(rst));  // open: Qn, en, reset
  or or_1 (or_1_out, demultiplexer_4_out0, insbeg, DO2, begins);
  Demultiplexer #(.enable("false")) demultiplexer_1 (.out0(demultiplexer_1_out0), .out1(holdstop), .in(a), .sel(halt));
  or or_2 (or_2_out, memwait, demultiplexer_5_out0);
  Demultiplexer #(.enable("false")) demultiplexer_2 (
    .out0(begins), .out1(demultiplexer_2_out1), .in(d_ff_1_q), .sel(rst));
  D_Flip_Flop #(.trigger("falling")) d_ff_2 (
    .clk(clk), .D(or_1_out), .Q(loadInst_t), .reset(rst));  // open: Qn, preset, en
  Demultiplexer #(.enable("false")) demultiplexer_3 (.out0(DO2), .out1(memwait), .in(demultiplexer_1_out0), .sel(RAM));
  D_Flip_Flop #(.trigger("falling")) d_ff_3 (
    .clk(clk), .D(or_2_out), .Q(loadRam), .reset(rst));  // open: Qn, preset, en
  or or_3 (or_3_out, holdstop, stop);
  Clock clock_1 ();  // open: out
  or or_4 (INST, loadInst_t, demultiplexer_4_out0);
  Demultiplexer #(.enable("false")) demultiplexer_4 (
    .out0(demultiplexer_4_out0), .out1(a), .in(loadInst_t), .sel(\end ));
  Demultiplexer #(.enable("false")) demultiplexer_5 (
    .out0(demultiplexer_5_out0), .out1(insbeg), .in(loadRam), .sel(\end ));
  D_Flip_Flop #(.trigger("falling")) d_ff_4 (.clk(clk), .D(or_3_out), .Q(stop), .reset(rst));  // open: Qn, preset, en
  Multiplexer #(.width(4), .enable("false")) multiplexer_1 (
    .in0(RAMReadT), .in1(RAMWriteT), .out(timeram), .sel(writ_t));
  or or_5 (or_5_out, DO1, LoadInst);
  and and_1 (DO1, loadRam, rum);
  and and_2 (LoadInst, loadInst_t, rum);
  or or_6 (or_6_out, loadRam, loadInst_t);
  or or_7 (chip_select, loadInst_t, loadRam);
  and and_3 (writ, DO1, writ_t);
  and and_4 (storecache, or_5_out, ~writ_t, ~CACHERESPONSE);  // AND_Gate
  awaiter awaiter_1 (.in_2(timewait), .\end (\end ), .start(or_6_out), .clk(clk), .\do (rum));
  or or_8 (RUN, DO1, DO2);
  and and_5 (writ_t, ~loadInst_t, R0_W1);  // AND_Gate
  and and_6 (and_6_out, DO1, ~writ_t);  // AND_Gate
  Multiplexer #(.width(4), .enable("false")) multiplexer_2 (
    .in0(timeram), .in1(4'b0001), .out(timewait), .sel(and_7_out));
  and and_7 (and_7_out, CACHERESPONSE, ~writ_t);  // AND_Gate
  or or_9 (or_9_out, and_6_out, LoadInst);
  and and_8 (and_8_out, or_9_out, CACHERESPONSE);
  or or_10 (or_10_out, DO1, LoadInst);
  and and_9 (and_9_out, or_10_out, ~CACHERESPONSE);  // AND_Gate
  Counter #(.width(32), .max('hffffffff)) counter_1 (
    .count(and_8_out), .Q(HITS), .clk(and_8_out), .clr(rst));  // open: load, D, carry
  Counter #(.width(32), .max('hffffffff)) counter_2 (
    .count(and_9_out), .Q(MISSES), .clk(and_9_out), .clr(rst));  // open: load, D, carry

  // Other names for the same wires on the sheet: DO = RUN; LoadI = LoadInst; proc = DO2; RT[3:0] = RAMReadT;
  //   WT[3:0] = RAMWriteT
endmodule

module InstructionDecoder (
  input  [31:0] INST,
  input  LoadINstruction,
  input  clk,
  input  RST,
  input  KBD_AVAIL,
  output [4:0] Rs,
  output jr,
  output [4:0] Rt,
  output [3:0] toalu,
  output halt,
  output [4:0] Rd,
  output tty,
  output kbd,
  output rnd,
  output push,
  output pop,
  output beq,
  output bne,
  output blez,
  output bgtz,
  output bltz,
  output j,
  output lw,
  output sw,
  output [31:0] cte,
  output useCTE,
  output [31:0] offset,
  output [25:0] destino,
  output Write,
  output fromRAM,
  output RAM,
  output toRAM,
  output _11op,
  output toRT
);

  wire and_1_out, \logic , lw_sw, or_1_out, push_pop, write11, writealu;
  wire [1:0] DECOP;
  wire [3:0] func000000decode_1_output, opcode111111dec_1_output, opdisctinctdecode_1_output;
  wire [4:0] x;
  wire [5:0] FUNC, OP;
  wire [31:0] register_1_q;

  OPDECODE opdecode_1 (.in_1(OP), .Output(DECOP));
  Register #(.width(32), .trigger("falling")) register_1 (
    .D(INST), .en(LoadINstruction), .Q(register_1_q), .clk(clk), .clr(RST));
  InstSeparator instseparator_1 (.in_1(register_1_q), .OPcode(OP), .Rs(Rs), .Rt(Rt), .Rd(Rd), .x(x), .FUNCode(FUNC));
  // Probe on register_1_q
  OPDisctinctDECODE opdisctinctdecode_1 (.in_1(OP), .Output(opdisctinctdecode_1_output));
  and and_1 (and_1_out, KBD_AVAIL, kbd);
  FUNC000000DECODE func000000decode_1 (.in_1(FUNC), .Output(func000000decode_1_output));
  OPCODE111111dec opcode111111dec_1 (.in_1(FUNC), .Output(opcode111111dec_1_output));
  or or_1 (or_1_out, and_1_out, rnd);
  Multiplexer #(.select(2), .width(4), .enable("false")) multiplexer_1 (
    .in0(func000000decode_1_output), .in1(opdisctinctdecode_1_output), .in2(4'b0000),
    .in3(opcode111111dec_1_output), .out(toalu), .sel(DECOP));
  writealucountingsw writealucountingsw_1 (.ARIT(toalu), .sw(sw), .write00n01(writealu));
  push_pop push_pop_1 (.OP(DECOP), .FUNC(FUNC), .push(push), .pop(pop));
  branch branch_1 (.in_1(OP), .beq(beq), .bne(bne), .blez(blez), .bgtz(bgtz), .bltz(bltz), .j(j));
  lwsw lwsw_1 (.in_1(OP), .lw(lw), .sw(sw));
  Const const_1 (.in_2(Rd), .in_3(x), .in_4(FUNC), .Output(cte), .\logic (\logic ));
  Offst offst_1 (.in_1(Rd), .in_2(x), .in_3(FUNC), .Output(offset));
  destinosalto destinosalto_1 (.fx(FUNC), .x(x), .Rd(Rd), .Rt(Rt), .Rs(Rs), .Output(destino));
  jr jr_1 (.in_1(toalu), .jr(jr));
  islogic islogic_1 (.in_1(toalu), .islogic(\logic ));
  or or_2 (Write, writealu, or_1_out, lw, pop);
  or or_3 (fromRAM, pop, lw);
  or or_4 (toRAM, sw, push);
  and and_2 (_11op, DECOP[0], DECOP[1]);
  and and_3 (toRT, DECOP[0], ~DECOP[1]);  // AND_Gate
  or or_5 (lw_sw, lw, sw);
  or or_6 (RAM, fromRAM, toRAM);
  writewith11 writewith11_1 (.OP(DECOP), .ARIT(toalu), .write(write11), .halt(halt), .tty(tty), .kbd(kbd), .rnd(rnd));
  or or_7 (push_pop, push, pop);
  useCTE usecte_1 (.in_1(DECOP), .beq(beq), .bne(bne), .cte(useCTE));

  // Other names for the same wires on the sheet: AL[3:0] = toalu
endmodule

module DataPath (
  input  ram1_reg0,
  input  _11op,
  input  Rt,
  input  cte1_register0,
  input  R,
  input  W,
  input  [4:0] Rs,
  input  [4:0] Rt_2,
  input  [4:0] Rd,
  input  clk,
  input  [31:0] cte,
  input  RUN,
  input  [3:0] alusel,
  input  pop,
  input  [31:0] memory,
  input  push,
  input  [6:0] kbd,
  output eq,
  output lez,
  output ltz,
  output [31:0] RsO,
  output [6:0] tty,
  output [31:0] RtO,
  output [31:0] ALUO,
  output [31:0] SP,
  output [31:0] SP_4
);

  wire and_3_out, pop_t, push_t;
  wire [4:0] multiplexer_2_out;
  wire [31:0] multiplexer_1_out, multiplexer_3_out;

  Multiplexer #(.width(32), .enable("false")) multiplexer_1 (
    .in0(ALUO), .in1(memory), .out(multiplexer_1_out), .sel(ram1_reg0));
  Multiplexer #(.width(5), .disabled(0), .enable("false")) multiplexer_2 (
    .in0(Rd), .in1(Rt_2), .out(multiplexer_2_out), .sel(Rt));
  and and_1 (pop_t, RUN, pop);
  and and_2 (push_t, RUN, push);
  RegFile regfile_1 (
    .CLK(clk), .RST(R), .DI(multiplexer_1_out), .RW(and_3_out), .LS(multiplexer_2_out), .SA(Rs), .A(RsO),
    .B(RtO), .SB(Rt_2), .push(push_t), .pop(pop_t), .SP(SP), .SP_4(SP_4));
  and and_3 (and_3_out, RUN, W);
  Multiplexer #(.width(32), .disabled(0), .enable("false")) multiplexer_3 (
    .in0(RtO), .in1(cte), .out(multiplexer_3_out), .sel(cte1_register0));
  ALU alu_1 (
    .A(RsO), .B(multiplexer_3_out), .SEL(alusel), .out_11(ALUO), .clk(clk), .eq(eq), .lez(lez), .ltz(ltz),
    .kbd(kbd), ._11op(_11op), .RUN(RUN));
  tty tty_1 (.\input (RsO), .out_2(tty));

  // Other names for the same wires on the sheet: alus[3:0] = alusel; c = clk; ram[31:0] = memory; Rt_t[4:0] = Rt_2
endmodule

module BranchControl (
  input  [31:0] RIN,
  input  clk,
  input  R,
  input  [31:0] offIN,
  input  L_RUN,
  input  [25:0] destino,
  input  beq,
  input  eq,
  input  bne,
  input  blez,
  input  lez,
  input  bgtz,
  input  bltz,
  input  ltz,
  input  j,
  input  jr,
  output [31:0] Output
);

  wire and_1_out, and_2_out, and_3_out, and_4_out, and_5_out, b, cond, jr_j, not_1_out, not_2_out;
  wire [31:0] destinosalto, multiplexer_1_out, multiplexer_2_out;

  Multiplexer #(.width(32), .enable("false")) multiplexer_1 (
    .in0(RIN), .in1(destinosalto), .out(multiplexer_1_out), .sel(j));
  Multiplexer #(.width(32), .enable("false")) multiplexer_2 (
    .in0(multiplexer_1_out), .in1(offIN), .out(multiplexer_2_out), .sel(b));
  destinobuilder destinobuilder_1 (.des(destino), .PC(Output), .Output(destinosalto));
  and and_1 (and_1_out, beq, eq);
  and and_2 (and_2_out, bne, not_1_out);
  not not_1 (not_1_out, eq);
  and and_3 (and_3_out, blez, lez);
  and and_4 (and_4_out, bgtz, not_2_out);
  not not_2 (not_2_out, lez);
  and and_5 (and_5_out, bltz, ltz);
  PC pc_1 (.IN(multiplexer_2_out), .Output(Output), .jr_j(jr_j), .l(L_RUN), .clk(clk), .r(R), .cond(cond));
  or or_1 (cond, and_1_out, and_2_out, and_3_out, and_4_out, and_5_out);
  or or_2 (jr_j, j, jr);
  not not_3 (b, jr_j);

  // Other names for the same wires on the sheet: PC[31:0] = Output
endmodule

module RAMInterface (
  input  INST,
  input  sw,
  input  push,
  input  [31:0] PC,
  input  pop,
  input  [31:0] ALUO,
  input  [31:0] SP___4,
  input  [31:0] SP,
  input  [31:0] Rs,
  input  [31:0] Rt,
  input  [31:0] fromRAM1,
  input  [31:0] fromRAM2,
  input  [31:0] fromRAM3,
  input  [31:0] fromRAM4,
  input  [31:0] CACHEOUTPUT,
  input  CACHERESPONSE,
  output [1:0] sel,
  output [3:0] mask,
  output [15:0] addr,
  output [31:0] toRAM,
  output [31:0] fromRAM
);

  wire not_1_out, push_pop;
  wire [31:0] multiplexer_1_out, multiplexer_2_out, multiplexer_3_out, multiplexer_4_out, multiplexer_5_out,
       multiplexer_6_out;

  or or_1 (push_pop, push, pop);
  Multiplexer #(.width(32), .enable("false")) multiplexer_1 (.in0(Rs), .in1(Rt), .out(multiplexer_1_out), .sel(sw));
  Multiplexer #(.width(32), .enable("false")) multiplexer_2 (
    .in0(ALUO), .in1(SP___4), .out(multiplexer_2_out), .sel(push_pop));
  big_to_low big_to_low_1 (.in_1(multiplexer_1_out), .Output(toRAM));
  Multiplexer #(.select(2), .width(32), .enable("false")) multiplexer_3 (
    .in0(fromRAM1), .in1(fromRAM2), .in2(fromRAM3), .in3(fromRAM4), .out(multiplexer_3_out), .sel(sel));
  Multiplexer #(.width(32), .enable("false")) multiplexer_4 (
    .in0(multiplexer_2_out), .in1(SP), .out(multiplexer_4_out), .sel(pop));
  Multiplexer #(.width(32), .enable("false")) multiplexer_5 (
    .in0(PC), .in1(multiplexer_4_out), .out(multiplexer_5_out), .sel(not_1_out));
  not not_1 (not_1_out, INST);
  big_to_low big_to_low_2 (.in_1(multiplexer_6_out), .Output(fromRAM));
  Multiplexer #(.width(32), .enable("false")) multiplexer_6 (
    .in0(multiplexer_3_out), .in1(CACHEOUTPUT), .out(multiplexer_6_out), .sel(CACHERESPONSE));
  addrnmask addrnmask_1 (.in_1(multiplexer_5_out), .mask(mask), .masksel(sel), .addr(addr));

  // Other names for the same wires on the sheet: fR1[31:0] = fromRAM1; fR2[31:0] = fromRAM2; fR3[31:0] = fromRAM3;
  //   fR4[31:0] = fromRAM4
endmodule

module Cache (
  input  RW,
  input  rst,
  input  clk,
  input  [15:0] addr,
  input  [1:0] sel,
  input  store,
  input  [31:0] DI0,
  input  [31:0] DI1,
  input  CACHEENABLE,
  input  [31:0] DI2,
  input  [31:0] DI3,
  input  [31:0] toRAM,
  output [31:0] CACHEOut,
  output CACHERESPONSE
);

  wire and_1_out, and_2_out, and_3_out, and_5_out, and_6_out, comparator_1_eq, s1, s2, s3, s4, s10, s11, s20,
       s21, s30, s31, s40, s41, store0, store1, valid, valid0, valid1, w1, w2, w3, w4;
  wire [4:0] addr_t;
  wire [10:0] tagin, tagout, tagout0, tagout1;
  wire [31:0] DI0_t, DI1_t, DI2_t, DI3_t, O00, O01, O10, O11, O20, O21, O30, O31, Out0, Out1;

  and and_1 (and_1_out, w1, CACHERESPONSE);
  or or_1 (s1, and_1_out, store);
  CacheBank32 cachebank32_1 (.D(DI0_t), .c(clk), .r(rst), .RW(s10), .LS(addr_t), .OUTPUT(O00));
  CacheBank32 cachebank32_2 (.D(DI0_t), .c(clk), .r(rst), .RW(s11), .LS(addr_t), .OUTPUT(O01));
  adrrtoselntag adrrtoselntag_1 (.addr(addr), .tag(tagin), .selector(addr_t));
  Multiplexer #(.width(32), .enable("false")) multiplexer_1 (.in0(DI0), .in1(toRAM), .out(DI0_t), .sel(RW));
  Multiplexer #(.width(32), .enable("false")) multiplexer_2 (.in0(DI1), .in1(toRAM), .out(DI1_t), .sel(RW));
  Multiplexer #(.width(32), .enable("false")) multiplexer_3 (.in0(DI2), .in1(toRAM), .out(DI2_t), .sel(RW));
  Multiplexer #(.width(32), .enable("false")) multiplexer_4 (.in0(DI3), .in1(toRAM), .out(DI3_t), .sel(RW));
  and and_2 (and_2_out, w2, CACHERESPONSE);
  or or_2 (s2, and_2_out, store);
  CacheBank32 cachebank32_3 (.D(DI1_t), .c(clk), .r(rst), .RW(s20), .LS(addr_t), .OUTPUT(O10));
  CacheBank32 cachebank32_4 (.D(DI1_t), .c(clk), .r(rst), .RW(s21), .LS(addr_t), .OUTPUT(O11));
  Comparator #(.width(11), .mode("unsigned")) comparator_1 (
    .a(tagout), .b(tagin), .eq(comparator_1_eq));  // open: gt, lt
  and and_3 (and_3_out, comparator_1_eq, valid);
  and and_4 (CACHERESPONSE, and_3_out, CACHEENABLE);
  Multiplexer #(.select(2), .width(32), .enable("false")) multiplexer_5 (
    .in0(O00), .in1(O10), .in2(O20), .in3(O30), .out(Out0), .sel(sel));
  Multiplexer #(.select(2), .width(32), .enable("false")) multiplexer_6 (
    .in0(O01), .in1(O11), .in2(O21), .in3(O31), .out(Out1), .sel(sel));
  and and_5 (and_5_out, w3, CACHERESPONSE);
  or or_3 (s3, and_5_out, store);
  CacheBank32 cachebank32_5 (.D(DI2_t), .c(clk), .r(rst), .RW(s30), .LS(addr_t), .OUTPUT(O20));
  CacheBank32 cachebank32_6 (.D(DI2_t), .c(clk), .r(rst), .RW(s31), .LS(addr_t), .OUTPUT(O21));
  CacheBank11 cachebank11_1 (.D(tagin), .c(clk), .r(rst), .RW(store0), .LS(addr_t), .OUTPUT(tagout0));
  CacheBank11 cachebank11_2 (.D(tagin), .c(clk), .r(rst), .RW(store1), .LS(addr_t), .OUTPUT(tagout1));
  Multiplexer #(.width(32), .enable("false")) multiplexer_7 (.in0(Out0), .in1(Out1), .out(CACHEOut), .sel(addr[5]));
  and and_6 (and_6_out, w4, CACHERESPONSE);
  or or_4 (s4, and_6_out, store);
  CacheBank32 cachebank32_7 (.D(DI3_t), .c(clk), .r(rst), .RW(s40), .LS(addr_t), .OUTPUT(O30));
  CacheBank32 cachebank32_8 (.D(DI3_t), .c(clk), .r(rst), .RW(s41), .LS(addr_t), .OUTPUT(O31));
  CacheBank1 cachebank1_1 (.D(1'b1), .c(clk), .r(rst), .RW(store0), .LS(addr_t), .OUTPUT(valid0));
  CacheBank1 cachebank1_2 (.D(1'b1), .c(clk), .r(rst), .RW(store1), .LS(addr_t), .OUTPUT(valid1));
  Demultiplexer #(.enable("false")) demultiplexer_1 (.out0(store0), .out1(store1), .in(store), .sel(addr[5]));
  Demultiplexer #(.select(2), .enable("false")) demultiplexer_2 (
    .out0(w1), .out1(w2), .out2(w3), .out3(w4), .in(RW), .sel(sel));
  Multiplexer #(.enable("false")) multiplexer_8 (.in0(valid0), .in1(valid1), .out(valid), .sel(addr[5]));
  Demultiplexer #(.enable("false")) demultiplexer_3 (.out0(s10), .out1(s11), .in(s1), .sel(addr[5]));
  Demultiplexer #(.enable("false")) demultiplexer_4 (.out0(s20), .out1(s21), .in(s2), .sel(addr[5]));
  Demultiplexer #(.enable("false")) demultiplexer_5 (.out0(s30), .out1(s31), .in(s3), .sel(addr[5]));
  Demultiplexer #(.enable("false")) demultiplexer_6 (.out0(s40), .out1(s41), .in(s4), .sel(addr[5]));
  Multiplexer #(.width(11), .enable("false")) multiplexer_9 (.in0(tagout0), .in1(tagout1), .out(tagout), .sel(addr[5]));

  // Other names for the same wires on the sheet: frag = addr[5]; Cresp = CACHERESPONSE; D0[31:0] = DI0;
  //   D1[31:0] = DI1; D2[31:0] = DI2; D3[31:0] = DI3; selout[1:0] = sel; TR[31:0] = toRAM

  // Notes on the sheet:
  //   BANKS
  //   TAG
  //   TAG
  //   VALID
  //   VALID
endmodule

module PC (
  input  [31:0] IN,
  input  l,
  input  clk,
  input  r,
  input  jr_j,
  input  cond,
  output [31:0] Output
);

  wire [31:0] adder_1_out, adder_2_out, multiplexer_1_out, multiplexer_2_out;

  // Probe on multiplexer_1_out
  Multiplexer #(.width(32), .enable("false")) multiplexer_1 (
    .in0(adder_2_out), .in1(IN), .out(multiplexer_1_out), .sel(jr_j));
  Register #(.width(32), .trigger("falling")) register_1 (
    .D(multiplexer_1_out), .en(l), .Q(Output), .clk(clk), .clr(r));
  Multiplexer #(.width(32), .enable("false")) multiplexer_2 (
    .in0(32'h4), .in1(adder_1_out), .out(multiplexer_2_out), .sel(cond));
  Adder #(.width(32)) adder_1 (.a(IN), .b(32'h4), .out(adder_1_out));  // open: cin, cout
  Adder #(.width(32)) adder_2 (.a(Output), .b(multiplexer_2_out), .out(adder_2_out));  // open: cin, cout

  // Other names for the same wires on the sheet: off[31:0] = IN
endmodule

module RegFile (
  input  CLK,
  input  RST,
  input  [31:0] DI,
  input  push,
  input  pop,
  input  RW,
  input  [4:0] LS,
  input  [4:0] SA,
  input  [4:0] SB,
  output [31:0] SP,
  output [31:0] SP_4,
  output [31:0] A,
  output [31:0] B
);

  wire l0, l1, l2, l3, l4, l5, l6, l7, l8, l9, l10, l11, l12, l13, l14, l15, l16, l17, l18, l19, l20, l21,
       l22, l23, l24, l25, l26, l27, l28, l29, l30, l31;
  wire [31:0] r1, r2, r3, r4, r5, r6, r7, r8, r9, r10, r11, r12, r13, r14, r15, r16, r17, r18, r19, r20, r21,
       r22, r23, r24, r25, r26, r27, r28, r29, r30;

  Demultiplexer #(.select(5), .disabled(0)) demultiplexer_1 (
    .out0(l0), .out1(l1), .out2(l2), .out3(l3), .out4(l4), .out5(l5), .out6(l6), .out7(l7), .out8(l8),
    .out9(l9), .out10(l10), .out11(l11), .out12(l12), .out13(l13), .out14(l14), .out15(l15), .out16(l16),
    .out17(l17), .out18(l18), .out19(l19), .out20(l20), .out21(l21), .out22(l22), .out23(l23), .out24(l24),
    .out25(l25), .out26(l26), .out27(l27), .out28(l28), .out29(l29), .out30(l30), .out31(l31), .in(1'b1),
    .sel(LS), .en(RW));
  Register #(.width(32), .trigger("falling")) register_1 (.D(DI), .en(l8), .Q(r8), .clk(CLK), .clr(RST));
  Register #(.width(32), .trigger("falling")) register_2 (.D(DI), .en(l16), .Q(r16), .clk(CLK), .clr(RST));
  Register #(.width(32), .trigger("falling")) register_3 (.D(DI), .en(l24), .Q(r24), .clk(CLK), .clr(RST));
  Register #(.width(32), .trigger("falling")) register_4 (.D(DI), .en(l1), .Q(r1), .clk(CLK), .clr(RST));
  Register #(.width(32), .trigger("falling")) register_5 (.D(DI), .en(l9), .Q(r9), .clk(CLK), .clr(RST));
  Register #(.width(32), .trigger("falling")) register_6 (.D(DI), .en(l17), .Q(r17), .clk(CLK), .clr(RST));
  Register #(.width(32), .trigger("falling")) register_7 (.D(DI), .en(l25), .Q(r25), .clk(CLK), .clr(RST));
  Register #(.width(32), .trigger("falling")) register_8 (.D(DI), .en(l2), .Q(r2), .clk(CLK), .clr(RST));
  Register #(.width(32), .trigger("falling")) register_9 (.D(DI), .en(l10), .Q(r10), .clk(CLK), .clr(RST));
  Register #(.width(32), .trigger("falling")) register_10 (.D(DI), .en(l18), .Q(r18), .clk(CLK), .clr(RST));
  Register #(.width(32), .trigger("falling")) register_11 (.D(DI), .en(l26), .Q(r26), .clk(CLK), .clr(RST));
  Register #(.width(32), .trigger("falling")) register_12 (.D(DI), .en(l3), .Q(r3), .clk(CLK), .clr(RST));
  Register #(.width(32), .trigger("falling")) register_13 (.D(DI), .en(l11), .Q(r11), .clk(CLK), .clr(RST));
  Register #(.width(32), .trigger("falling")) register_14 (.D(DI), .en(l19), .Q(r19), .clk(CLK), .clr(RST));
  Register #(.width(32), .trigger("falling")) register_15 (.D(DI), .en(l27), .Q(r27), .clk(CLK), .clr(RST));
  Multiplexer #(.select(5), .width(32), .enable("false")) multiplexer_1 (
    .in0({32{1'b0}}), .in1(r1), .in2(r2), .in3(r3), .in4(r4), .in5(r5), .in6(r6), .in7(r7), .in8(r8),
    .in9(r9), .in10(r10), .in11(r11), .in12(r12), .in13(r13), .in14(r14), .in15(r15), .in16(r16), .in17(r17),
    .in18(r18), .in19(r19), .in20(r20), .in21(r21), .in22(r22), .in23(r23), .in24(r24), .in25(r25),
    .in26(r26), .in27(r27), .in28(r28), .in29(r29), .in30(r30), .in31(SP), .out(A), .sel(SA));
  Register #(.width(32), .trigger("falling")) register_16 (.D(DI), .en(l4), .Q(r4), .clk(CLK), .clr(RST));
  Register #(.width(32), .trigger("falling")) register_17 (.D(DI), .en(l12), .Q(r12), .clk(CLK), .clr(RST));
  Register #(.width(32), .trigger("falling")) register_18 (.D(DI), .en(l20), .Q(r20), .clk(CLK), .clr(RST));
  Register #(.width(32), .trigger("falling")) register_19 (.D(DI), .en(l28), .Q(r28), .clk(CLK), .clr(RST));
  Register #(.width(32), .trigger("falling")) register_20 (.D(DI), .en(l5), .Q(r5), .clk(CLK), .clr(RST));
  Register #(.width(32), .trigger("falling")) register_21 (.D(DI), .en(l13), .Q(r13), .clk(CLK), .clr(RST));
  Register #(.width(32), .trigger("falling")) register_22 (.D(DI), .en(l21), .Q(r21), .clk(CLK), .clr(RST));
  Register #(.width(32), .trigger("falling")) register_23 (.D(DI), .en(l29), .Q(r29), .clk(CLK), .clr(RST));
  Register #(.width(32), .trigger("falling")) register_24 (.D(DI), .en(l6), .Q(r6), .clk(CLK), .clr(RST));
  Register #(.width(32), .trigger("falling")) register_25 (.D(DI), .en(l14), .Q(r14), .clk(CLK), .clr(RST));
  Register #(.width(32), .trigger("falling")) register_26 (.D(DI), .en(l22), .Q(r22), .clk(CLK), .clr(RST));
  Register #(.width(32), .trigger("falling")) register_27 (.D(DI), .en(l30), .Q(r30), .clk(CLK), .clr(RST));
  Multiplexer #(.select(5), .width(32), .enable("false")) multiplexer_2 (
    .in0({32{1'b0}}), .in1(r1), .in2(r2), .in3(r3), .in4(r4), .in5(r5), .in6(r6), .in7(r7), .in8(r8),
    .in9(r9), .in10(r10), .in11(r11), .in12(r12), .in13(r13), .in14(r14), .in15(r15), .in16(r16), .in17(r17),
    .in18(r18), .in19(r19), .in20(r20), .in21(r21), .in22(r22), .in23(r23), .in24(r24), .in25(r25),
    .in26(r26), .in27(r27), .in28(r28), .in29(r29), .in30(r30), .in31(SP), .out(B), .sel(SB));
  Register #(.width(32), .trigger("falling")) register_28 (.D(DI), .en(l7), .Q(r7), .clk(CLK), .clr(RST));
  Register #(.width(32), .trigger("falling")) register_29 (.D(DI), .en(l15), .Q(r15), .clk(CLK), .clr(RST));
  Register #(.width(32), .trigger("falling")) register_30 (.D(DI), .en(l23), .Q(r23), .clk(CLK), .clr(RST));
  SP sp_1 (.di(DI), .l(l31), .r31(SP), .c(CLK), .r(RST), .push(push), .pop(pop), .SP_4(SP_4));

  // Other names for the same wires on the sheet: c = CLK; r = RST; r31[31:0] = SP
endmodule

module SP (
  input  push,
  input  pop,
  input  [31:0] di,
  input  c,
  input  r,
  input  l,
  output [31:0] r31,
  output [31:0] SP_4
);

  wire load, reg0op1, sum1sub0;
  wire [31:0] adder_1_out, multiplexer_1_out, multiplexer_2_out, opp;

  or or_1 (load, l, reg0op1);
  sumrestsp sumrestsp_1 (.push(push), .pop(pop), .sumrest(sum1sub0), .sumrestreg(reg0op1));
  Multiplexer #(.width(32), .disabled(0), .enable("false")) multiplexer_1 (
    .in0(di), .in1(opp), .out(multiplexer_1_out), .sel(reg0op1));
  Register #(.width(32), .trigger("falling")) register_1 (.D(multiplexer_1_out), .en(load), .Q(r31), .clk(c), .clr(r));
  Multiplexer #(.width(32), .disabled(0), .enable("false")) multiplexer_2 (
    .in0(r31), .in1(di), .out(multiplexer_2_out), .sel(l));
  Adder #(.width(32)) adder_1 (.a(multiplexer_2_out), .b(32'h4), .out(adder_1_out));  // open: cin, cout
  Subtractor #(.width(32)) subtractor_1 (.a(r31), .b(32'h4), .out(SP_4));  // open: bin, bout
  Multiplexer #(.width(32), .disabled(0), .enable("false")) multiplexer_3 (
    .in0(SP_4), .in1(adder_1_out), .out(opp), .sel(sum1sub0));
endmodule

module ALU (
  input  [31:0] A,
  input  [31:0] B,
  input  clk,
  input  [3:0] SEL,
  input  _11op,
  input  RUN,
  input  [6:0] kbd,
  output eq,
  output lez,
  output ltz,
  output [31:0] out_11
);

  wire and_2_out, comparator_1_lt, comparator_2_lt, comparator_3_eq, hilo, hilo_1_divmul;
  wire [1:0] hisel;
  wire [31:0] \and , divhi, divlo, divuhi, divulo, hi, kbd_t, low, multhi, multiplexer_2_out,
       multiplexer_3_out, multlo, muluhi, mululo, \nor , \or , rnd, slt, sltu, tunnel, tunnel_t, \xor ;

  Random #(.width(32)) random_1 (.clk(clk), .next(1'b1), .out(rnd));  // open: clr
  kbd kbd_1 (.in_1(kbd), .Output(kbd_t));
  Adder #(.width(32)) adder_1 (.a(A), .b(B), .out(tunnel));  // open: cin, cout
  Subtractor #(.width(32)) subtractor_1 (.a(A), .b(B), .out(tunnel_t));  // open: bin, bout
  Multiplier #(.width(32)) multiplier_1 (.a(A), .b(B), .out(mululo), .cout(muluhi));  // open: cin
  Divider #(.width(32)) divider_1 (.a(A), .b(B), .out(divulo), .rem(divuhi));  // open: upper
  MULTs mults_1 (.in_1(A), .B(B), .Output(multlo), .Output_2(multhi));
  DIVs divs_1 (.A(A), .B(B), .out(divlo), .rest(divhi));
  Comparator #(.width(32)) comparator_1 (.a(A), .b(B), .eq(eq), .lt(comparator_1_lt));  // open: gt
  Comparator #(.width(32), .mode("unsigned")) comparator_2 (.a(A), .b(B), .lt(comparator_2_lt));  // open: gt, eq
  concat concat_1 (.in_1(comparator_1_lt), .Output(slt));
  concat concat_2 (.in_1(comparator_2_lt), .Output(sltu));
  assign \and  = A & B;  // AND_Gate and_1, 32 bits wide
  assign \or  = A | B;  // OR_Gate or_1, 32 bits wide
  assign \nor  = ~(A | B);  // NOR_Gate nor_1, 32 bits wide
  assign \xor  = A ^ B;  // XOR_Gate xor_1, 32 bits wide
  Comparator #(.width(32)) comparator_3 (.a(A), .b({32{1'b0}}), .eq(comparator_3_eq), .lt(ltz));  // open: gt
  or or_2 (lez, comparator_3_eq, ltz);
  Multiplexer #(.select(4), .width(32), .enable("false")) multiplexer_1 (
    .in1(tunnel), .in2(tunnel_t), .in4(rnd), .in5(kbd_t), .in7(slt), .in8(sltu), .in9(\and ), .in10(\or ),
    .in11(\nor ), .in12(\xor ), .in13(A), .in14(hi), .in15(low), .out(out_11), .sel(SEL));  // open: in0, in3, in6
  Multiplexer #(.select(2), .width(32), .enable("false")) multiplexer_2 (
    .in0(multhi), .in1(muluhi), .in2(divhi), .in3(divuhi), .out(multiplexer_2_out), .sel(hisel));
  Multiplexer #(.select(2), .width(32), .enable("false")) multiplexer_3 (
    .in0(multlo), .in1(mululo), .in2(divlo), .in3(divulo), .out(multiplexer_3_out), .sel(hisel));
  mulu_divu mulu_divu_1 (.in_1(SEL), .Output(hisel));
  hilo hilo_1 (.in_1(SEL), .divmul(hilo_1_divmul));
  and and_2 (and_2_out, hilo_1_divmul, ~_11op);  // AND_Gate
  Register #(.width(32)) register_1 (.D(multiplexer_2_out), .en(hilo), .Q(hi), .clk(clk));  // open: clr
  Register #(.width(32)) register_2 (.D(multiplexer_3_out), .en(hilo), .Q(low), .clk(clk));  // open: clr
  and and_3 (hilo, and_2_out, RUN);

  // Other names for the same wires on the sheet: c = clk
endmodule

module InstSeparator (
  input  [31:0] in_1,
  output [5:0] OPcode,
  output [4:0] Rs,
  output [4:0] Rt,
  output [4:0] Rd,
  output [4:0] x,
  output [5:0] FUNCode
);


  assign FUNCode = in_1[5:0];
  assign OPcode = in_1[31:26];
  assign Rd = in_1[15:11];
  assign Rs = in_1[25:21];
  assign Rt = in_1[20:16];
  assign x = in_1[10:6];
endmodule

module OPDECODE (
  input  [5:0] in_1,
  output [1:0] Output
);

  wire and_1_out, and_2_out, and_3_out, and_4_out, and_5_out, not_1_out, not_2_out, not_3_out, not_4_out,
       not_5_out, not_6_out;

  not not_1 (not_1_out, in_1[2]);
  not not_2 (not_2_out, in_1[1]);
  not not_3 (not_3_out, in_1[0]);
  not not_4 (not_4_out, in_1[5]);
  not not_5 (not_5_out, in_1[3]);
  not not_6 (not_6_out, in_1[4]);
  and and_1 (and_1_out, in_1[5], in_1[4], in_1[3], not_1_out, not_2_out, not_3_out);
  and and_2 (and_2_out, in_1[5], in_1[4], in_1[3], in_1[2], in_1[1], in_1[0]);
  and and_3 (and_3_out, not_4_out, in_1[3]);
  and and_4 (and_4_out, in_1[4], not_5_out);
  and and_5 (and_5_out, in_1[5], not_6_out);
  or or_1 (Output[1], and_1_out, and_2_out);
  or or_2 (Output[0], in_1[0], in_1[1], in_1[2], and_3_out, and_4_out, and_5_out);
endmodule

module FUNC000000DECODE (
  input  [5:0] in_1,
  output [3:0] Output
);

  wire and_1_out, and_2_out, and_3_out, and_4_out, and_5_out, and_6_out, and_7_out, and_8_out, and_9_out,
       and_10_out, and_11_out, and_12_out, and_13_out, and_14_out, and_15_out, and_16_out, and_17_out,
       and_18_out, and_19_out, and_20_out, not_1_out, not_2_out, not_3_out, not_4_out, not_5_out, not_6_out,
       not_7_out, not_8_out, not_9_out, not_10_out, not_11_out, not_12_out, not_13_out, not_14_out,
       not_15_out, not_16_out, not_17_out, not_18_out, not_19_out, not_20_out, not_21_out, not_22_out,
       not_23_out, not_24_out, not_25_out, not_26_out, not_27_out, not_28_out, not_29_out, not_30_out,
       not_31_out, not_32_out, not_33_out, not_34_out, not_35_out, not_36_out, not_37_out, not_38_out,
       not_39_out, not_40_out, not_41_out, not_42_out, not_43_out, not_44_out, not_45_out, not_46_out,
       not_47_out, not_48_out, not_49_out, not_50_out, not_51_out, not_52_out, not_53_out, not_54_out,
       not_55_out, not_56_out, not_57_out, not_58_out, not_59_out, not_60_out, not_61_out, not_62_out;

  not not_1 (not_1_out, in_1[4]);
  not not_2 (not_2_out, in_1[2]);
  not not_3 (not_3_out, in_1[1]);
  not not_4 (not_4_out, in_1[0]);
  not not_5 (not_5_out, in_1[5]);
  not not_6 (not_6_out, in_1[3]);
  not not_7 (not_7_out, in_1[2]);
  not not_8 (not_8_out, in_1[0]);
  not not_9 (not_9_out, in_1[4]);
  not not_10 (not_10_out, in_1[3]);
  not not_11 (not_11_out, in_1[1]);
  not not_12 (not_12_out, in_1[4]);
  not not_13 (not_13_out, in_1[3]);
  not not_14 (not_14_out, in_1[4]);
  not not_15 (not_15_out, in_1[2]);
  not not_16 (not_16_out, in_1[4]);
  not not_17 (not_17_out, in_1[2]);
  not not_18 (not_18_out, in_1[1]);
  not not_19 (not_19_out, in_1[0]);
  not not_20 (not_20_out, in_1[5]);
  not not_21 (not_21_out, in_1[3]);
  not not_22 (not_22_out, in_1[2]);
  not not_23 (not_23_out, in_1[0]);
  not not_24 (not_24_out, in_1[5]);
  not not_25 (not_25_out, in_1[2]);
  not not_26 (not_26_out, in_1[0]);
  not not_27 (not_27_out, in_1[5]);
  not not_28 (not_28_out, in_1[2]);
  not not_29 (not_29_out, in_1[4]);
  not not_30 (not_30_out, in_1[2]);
  not not_31 (not_31_out, in_1[0]);
  not not_32 (not_32_out, in_1[5]);
  not not_33 (not_33_out, in_1[3]);
  not not_34 (not_34_out, in_1[2]);
  not not_35 (not_35_out, in_1[0]);
  not not_36 (not_36_out, in_1[5]);
  not not_37 (not_37_out, in_1[2]);
  not not_38 (not_38_out, in_1[1]);
  not not_39 (not_39_out, in_1[0]);
  not not_40 (not_40_out, in_1[5]);
  not not_41 (not_41_out, in_1[2]);
  not not_42 (not_42_out, in_1[4]);
  not not_43 (not_43_out, in_1[2]);
  not not_44 (not_44_out, in_1[0]);
  not not_45 (not_45_out, in_1[4]);
  not not_46 (not_46_out, in_1[3]);
  not not_47 (not_47_out, in_1[5]);
  not not_48 (not_48_out, in_1[2]);
  not not_49 (not_49_out, in_1[1]);
  not not_50 (not_50_out, in_1[0]);
  not not_51 (not_51_out, in_1[5]);
  not not_52 (not_52_out, in_1[2]);
  not not_53 (not_53_out, in_1[0]);
  not not_54 (not_54_out, in_1[4]);
  not not_55 (not_55_out, in_1[3]);
  not not_56 (not_56_out, in_1[1]);
  not not_57 (not_57_out, in_1[0]);
  not not_58 (not_58_out, in_1[4]);
  not not_59 (not_59_out, in_1[3]);
  not not_60 (not_60_out, in_1[4]);
  not not_61 (not_61_out, in_1[2]);
  not not_62 (not_62_out, in_1[0]);
  and and_1 (and_1_out, not_1_out, in_1[3], not_2_out, not_3_out, not_4_out);
  and and_2 (and_2_out, not_5_out, in_1[4], not_6_out, not_7_out, not_8_out);
  and and_3 (and_3_out, in_1[5], not_9_out, not_10_out, in_1[2], not_11_out);
  and and_4 (and_4_out, in_1[5], not_12_out, not_13_out, in_1[2], in_1[0]);
  and and_5 (and_5_out, in_1[5], not_14_out, in_1[3], not_15_out, in_1[1], in_1[0]);
  and and_6 (and_6_out, not_16_out, in_1[3], not_17_out, not_18_out, not_19_out);
  and and_7 (and_7_out, not_20_out, in_1[4], not_21_out, not_22_out, not_23_out);
  and and_8 (and_8_out, not_24_out, in_1[4], not_25_out, in_1[1], not_26_out);
  and and_9 (and_9_out, not_27_out, in_1[4], in_1[3], not_28_out, in_1[0]);
  and and_10 (and_10_out, in_1[5], not_29_out, in_1[3], not_30_out, not_31_out);
  and and_11 (and_11_out, not_32_out, in_1[4], not_33_out, not_34_out, not_35_out);
  and and_12 (and_12_out, not_36_out, in_1[4], not_37_out, not_38_out, not_39_out);
  and and_13 (and_13_out, not_40_out, in_1[4], in_1[3], not_41_out, in_1[1], in_1[0]);
  and and_14 (and_14_out, in_1[5], not_42_out, not_43_out, in_1[1], not_44_out);
  and and_15 (and_15_out, in_1[5], not_45_out, not_46_out, in_1[2], in_1[0]);
  and and_16 (and_16_out, not_47_out, in_1[3], not_48_out, not_49_out, not_50_out);
  and and_17 (and_17_out, not_51_out, in_1[4], not_52_out, in_1[1], not_53_out);
  and and_18 (and_18_out, in_1[5], not_54_out, not_55_out, not_56_out, not_57_out);
  and and_19 (and_19_out, in_1[5], not_58_out, not_59_out, in_1[2], in_1[1], in_1[0]);
  and and_20 (and_20_out, in_1[5], not_60_out, in_1[3], not_61_out, in_1[1], not_62_out);
  or or_1 (Output[3], and_1_out, and_2_out, and_3_out, and_4_out, and_5_out);
  or or_2 (Output[2], and_6_out, and_7_out, and_8_out, and_9_out, and_10_out);
  or or_3 (Output[1], and_11_out, and_12_out, and_13_out, and_14_out, and_15_out);
  or or_4 (Output[0], and_16_out, and_17_out, and_18_out, and_19_out, and_20_out);
endmodule

module OPDisctinctDECODE (
  input  [5:0] in_1,
  output [3:0] Output
);

  wire and_1_out, and_2_out, and_3_out, and_5_out, and_6_out, and_7_out, and_8_out, and_9_out, not_1_out,
       not_2_out, not_3_out, not_4_out, not_5_out, not_6_out, not_7_out, not_8_out, not_9_out, not_10_out,
       not_11_out, not_12_out, not_13_out, not_14_out, not_15_out, not_16_out, not_17_out, not_18_out,
       not_19_out, not_20_out, not_21_out, not_22_out, not_23_out, not_24_out, not_25_out, not_26_out,
       not_27_out, not_28_out, not_29_out;

  not not_1 (not_1_out, in_1[5]);
  not not_2 (not_2_out, in_1[4]);
  not not_3 (not_3_out, in_1[2]);
  not not_4 (not_4_out, in_1[5]);
  not not_5 (not_5_out, in_1[4]);
  not not_6 (not_6_out, in_1[1]);
  not not_7 (not_7_out, in_1[5]);
  not not_8 (not_8_out, in_1[4]);
  not not_9 (not_9_out, in_1[0]);
  not not_10 (not_10_out, in_1[5]);
  not not_11 (not_11_out, in_1[4]);
  not not_12 (not_12_out, in_1[0]);
  not not_13 (not_13_out, in_1[5]);
  not not_14 (not_14_out, in_1[4]);
  not not_15 (not_15_out, in_1[2]);
  not not_16 (not_16_out, in_1[0]);
  not not_17 (not_17_out, in_1[5]);
  not not_18 (not_18_out, in_1[4]);
  not not_19 (not_19_out, in_1[1]);
  not not_20 (not_20_out, in_1[5]);
  not not_21 (not_21_out, in_1[4]);
  not not_22 (not_22_out, in_1[2]);
  not not_23 (not_23_out, in_1[0]);
  not not_24 (not_24_out, in_1[5]);
  not not_25 (not_25_out, in_1[4]);
  not not_26 (not_26_out, in_1[1]);
  not not_27 (not_27_out, in_1[0]);
  not not_28 (not_28_out, in_1[4]);
  not not_29 (not_29_out, in_1[2]);
  and and_1 (and_1_out, not_1_out, not_2_out, in_1[3], not_3_out, in_1[1], in_1[0]);
  and and_2 (and_2_out, not_4_out, not_5_out, in_1[3], in_1[2], not_6_out);
  and and_3 (and_3_out, not_7_out, not_8_out, in_1[3], in_1[2], not_9_out);
  and and_4 (Output[2], not_10_out, not_11_out, in_1[3], in_1[1], not_12_out);
  and and_5 (and_5_out, not_13_out, not_14_out, in_1[3], not_15_out, in_1[1], not_16_out);
  and and_6 (and_6_out, not_17_out, not_18_out, in_1[3], in_1[2], not_19_out, in_1[0]);
  and and_7 (and_7_out, not_20_out, not_21_out, in_1[3], not_22_out, not_23_out);
  and and_8 (and_8_out, not_24_out, not_25_out, in_1[3], not_26_out, not_27_out);
  and and_9 (and_9_out, in_1[5], not_28_out, not_29_out, in_1[1], in_1[0]);
  or or_1 (Output[3], and_1_out, and_2_out, and_3_out);
  or or_2 (Output[1], and_5_out, and_6_out);
  or or_3 (Output[0], and_7_out, and_8_out, and_9_out);
endmodule

module Const (
  input  \logic ,
  input  [4:0] in_2,
  input  [4:0] in_3,
  input  [5:0] in_4,
  output [31:0] Output
);

  Multiplexer #(.enable("false")) multiplexer_1 (.in0(in_2[4]), .in1(1'b0), .out(Output[31]), .sel(\logic ));

  assign Output[30:0] = {{15{Output[31]}}, in_2, in_3, in_4};
endmodule

module concat (
  input  in_1,
  output [31:0] Output
);


  assign Output = {{31{1'b0}}, in_1};
endmodule

module hilo (
  input  [3:0] in_1,
  output divmul
);

  wire and_1_out, and_2_out, and_3_out, not_1_out, not_2_out, not_3_out, not_4_out, not_5_out, not_6_out;

  not not_1 (not_1_out, in_1[3]);
  not not_2 (not_2_out, in_1[2]);
  not not_3 (not_3_out, in_1[3]);
  not not_4 (not_4_out, in_1[1]);
  not not_5 (not_5_out, in_1[3]);
  not not_6 (not_6_out, in_1[0]);
  and and_1 (and_1_out, not_1_out, not_2_out, in_1[1], in_1[0]);
  and and_2 (and_2_out, not_3_out, in_1[2], not_4_out);
  and and_3 (and_3_out, not_5_out, in_1[2], not_6_out);
  or or_1 (divmul, and_1_out, and_2_out, and_3_out);
endmodule

module mulu_divu (
  input  [3:0] in_1,
  output [1:0] Output
);

  wire and_1_out, and_2_out, not_1_out, not_2_out;

  not not_1 (not_1_out, in_1[1]);
  and and_1 (and_1_out, not_1_out, in_1[0]);
  and and_2 (and_2_out, in_1[1], not_2_out);
  not not_2 (not_2_out, in_1[0]);
  not not_3 (Output[0], in_1[0]);
  or or_1 (Output[1], and_1_out, and_2_out);
endmodule

module Writefromalu (
  input  [3:0] in_1,
  output write
);

  wire and_1_out, and_2_out, and_3_out, and_4_out, and_5_out, not_1_out, not_2_out, not_3_out, not_4_out,
       not_5_out, not_6_out;

  not not_1 (not_1_out, in_1[2]);
  not not_2 (not_2_out, in_1[1]);
  not not_3 (not_3_out, in_1[2]);
  not not_4 (not_4_out, in_1[0]);
  not not_5 (not_5_out, in_1[2]);
  not not_6 (not_6_out, in_1[0]);
  and and_1 (and_1_out, not_1_out, not_2_out, in_1[0]);
  and and_2 (and_2_out, not_3_out, in_1[1], not_4_out);
  and and_3 (and_3_out, in_1[2], in_1[1], in_1[0]);
  and and_4 (and_4_out, in_1[3], not_5_out);
  and and_5 (and_5_out, in_1[3], not_6_out);
  or or_1 (write, and_1_out, and_2_out, and_3_out, and_4_out, and_5_out);
endmodule

module awaiter (
  input  start,
  input  [3:0] in_2,
  input  clk,
  output \do ,
  output \end 
);

  wire comparator_1_gt, or_1_out, or_2_out;
  wire [4:0] adder_1_out, counter_1_q;

  Adder #(.width(5)) adder_1 (.a({1'b0, in_2}), .b({5{1'b0}}), .out(adder_1_out));  // open: cin, cout
  or or_1 (or_1_out, start, or_2_out);
  Counter #(.width(5), .max('h1f), .ongoal("stay")) counter_1 (
    .load(or_1_out), .D(adder_1_out), .count(or_2_out), .Q(counter_1_q), .clk(clk));  // open: carry, clr
  Comparator #(.width(5), .mode("unsigned")) comparator_1 (
    .a(counter_1_q), .b(5'b00001), .gt(comparator_1_gt), .eq(\do ), .lt(\end ));
  or or_2 (or_2_out, comparator_1_gt, \do );

  // Notes on the sheet:
  //   Esto de sumarle 1 antes resulto innecesario en ultima instancia pero se quedan los 5 bits pq tampoco estorba, solo cambie por 0
endmodule

module push_pop (
  input  [1:0] OP,
  input  [5:0] FUNC,
  output push,
  output pop
);

  wire and_1_out;

  and and_1 (and_1_out, OP[1], ~OP[0]);  // AND_Gate
  and and_2 (push, and_1_out, FUNC[0]);
  and and_3 (pop, and_1_out, ~FUNC[0]);  // AND_Gate
endmodule

module SMIPSTEST (
  input  Kbd_Available,
  input  [6:0] Kbd_ASCII_Data,
  input  [31:0] RAM_Out_0,
  input  [15:0] in_4,
  input  [31:0] RAM_Out_1,
  input  Reset,
  input  [31:0] RAM_Out_2,
  input  Clock,
  input  [31:0] RAM_Out_3,
  input  [3:0] Read_Time,
  input  [3:0] Write_Time,
  output Kbd_Enable,
  output [15:0] Address,
  output Kbd_Clear,
  output TTY_Enable,
  output [6:0] TTY_ASCII_Data,
  output Stop,
  output [31:0] RAM_In_0,
  output [31:0] RAM_In_1,
  output [31:0] RAM_In_2,
  output [31:0] RAM_In_3,
  output [3:0] Mask,
  output nRead_Write,
  output Chip_Select
);


  assign Address = in_4;

  // Other names for the same wires on the sheet: CLK = Clock; CLR = Reset; CS = Chip_Select;
  //   KBD_AVAIL = Kbd_Available; KBD_CLR = Kbd_Clear; KBD_DATA[6:0] = Kbd_ASCII_Data; RAM_A[15:0] = in_4;
  //   RAM_INPUT_0[31:0] = RAM_In_0; RAM_INPUT_1[31:0] = RAM_In_1; RAM_INPUT_2[31:0] = RAM_In_2;
  //   RAM_INPUT_3[31:0] = RAM_In_3; RAM_MASK[3:0] = Mask; RAM_OUTPUT_0[31:0] = RAM_Out_0;
  //   RAM_OUTPUT_1[31:0] = RAM_Out_1; RAM_OUTPUT_2[31:0] = RAM_Out_2; RAM_OUTPUT_3[31:0] = RAM_Out_3;
  //   RW = nRead_Write; TTY_DATA[6:0] = TTY_ASCII_Data

  // Notes on the sheet:
  //   RAM ADDRESS
  //   DATA FROM RAM
  //   DATA TO RAM
  //   DATA WRITE MASK
  //   RAM TIMING
  //   RAM CONTROL
  //   KEYBOARD
  //   TTY
  //   SEQUENCING
endmodule

module jr (
  input  [3:0] in_1,
  output jr
);

  wire not_1_out;

  not not_1 (not_1_out, in_1[1]);
  and and_1 (jr, in_1[3], in_1[2], not_1_out, in_1[0]);
endmodule

module CacheObs (
  input  [5:0] index,
  input  in_2
);

  wire demultiplexer_1_out0, demultiplexer_1_out1;

  Demultiplexer #(.enable("false")) demultiplexer_1 (
    .out0(demultiplexer_1_out0), .out1(demultiplexer_1_out1), .in(1'b1), .sel(index[5]));
  Demultiplexer #(.select(5), .enable("false")) demultiplexer_2 (
    .in(demultiplexer_1_out0), .sel(index[4:0]));  // open: out0, out1, out2, out3, out4, out5, out6, out7, out8, out9, out10, out11, out12, out13, out14, out15, out16, out17, out18, out19, out20, out21, out22, out23, out24, out25, out26, out27, out28, out29, out30, out31
  Demultiplexer #(.select(5), .enable("false")) demultiplexer_3 (
    .in(demultiplexer_1_out1), .sel(index[4:0]));  // open: out0, out1, out2, out3, out4, out5, out6, out7, out8, out9, out10, out11, out12, out13, out14, out15, out16, out17, out18, out19, out20, out21, out22, out23, out24, out25, out26, out27, out28, out29, out30, out31

  // Other names for the same wires on the sheet: sel2[4:0] = index[4:0]
endmodule

module sumrestsp (
  input  push,
  input  pop,
  output sumrest,
  output sumrestreg
);

  wire and_2_out, and_3_out, not_1_out, not_2_out, not_3_out;

  not not_1 (not_1_out, push);
  not not_2 (not_2_out, push);
  not not_3 (not_3_out, pop);
  and and_1 (sumrest, not_1_out, pop);
  and and_2 (and_2_out, not_2_out, pop);
  and and_3 (and_3_out, push, not_3_out);
  or or_1 (sumrestreg, and_2_out, and_3_out);
endmodule

module Offst (
  input  [4:0] in_1,
  input  [4:0] in_2,
  input  [5:0] in_3,
  output [31:0] Output
);


  assign Output = {{15{in_1[4]}}, in_1[3:0], in_2, in_3, 2'b00};
endmodule

module islogic (
  input  [3:0] in_1,
  output islogic
);

  wire and_1_out, and_2_out, and_3_out, not_1_out, not_2_out, not_3_out, not_4_out;

  not not_1 (not_1_out, in_1[1]);
  not not_2 (not_2_out, in_1[0]);
  not not_3 (not_3_out, in_1[2]);
  and and_1 (and_1_out, in_1[3], not_3_out, in_1[0]);
  and and_2 (and_2_out, in_1[3], not_4_out, in_1[1]);
  not not_4 (not_4_out, in_1[2]);
  and and_3 (and_3_out, in_1[3], in_1[2], not_1_out, not_2_out);
  or or_1 (islogic, and_1_out, and_2_out, and_3_out);
endmodule

module branch (
  input  [5:0] in_1,
  output beq,
  output bne,
  output blez,
  output bgtz,
  output bltz,
  output j
);

  wire not_1_out, not_2_out, not_3_out, not_4_out, not_5_out, not_6_out, not_7_out, not_8_out, not_9_out,
       not_10_out, not_11_out, not_12_out, not_13_out, not_14_out, not_15_out, not_16_out, not_17_out,
       not_18_out, not_19_out, not_20_out, not_21_out, not_22_out, not_23_out, not_24_out, not_25_out,
       not_26_out;

  not not_1 (not_1_out, in_1[5]);
  not not_2 (not_2_out, in_1[4]);
  not not_3 (not_3_out, in_1[3]);
  not not_4 (not_4_out, in_1[1]);
  not not_5 (not_5_out, in_1[0]);
  not not_6 (not_6_out, in_1[5]);
  not not_7 (not_7_out, in_1[4]);
  not not_8 (not_8_out, in_1[3]);
  not not_9 (not_9_out, in_1[1]);
  not not_10 (not_10_out, in_1[5]);
  not not_11 (not_11_out, in_1[4]);
  not not_12 (not_12_out, in_1[3]);
  not not_13 (not_13_out, in_1[0]);
  not not_14 (not_14_out, in_1[5]);
  not not_15 (not_15_out, in_1[4]);
  not not_16 (not_16_out, in_1[3]);
  not not_17 (not_17_out, in_1[5]);
  not not_18 (not_18_out, in_1[4]);
  not not_19 (not_19_out, in_1[3]);
  not not_20 (not_20_out, in_1[2]);
  not not_21 (not_21_out, in_1[1]);
  not not_22 (not_22_out, in_1[5]);
  not not_23 (not_23_out, in_1[4]);
  not not_24 (not_24_out, in_1[3]);
  not not_25 (not_25_out, in_1[2]);
  not not_26 (not_26_out, in_1[0]);
  and and_1 (beq, not_1_out, not_2_out, not_3_out, in_1[2], not_4_out, not_5_out);
  and and_2 (bne, not_6_out, not_7_out, not_8_out, in_1[2], not_9_out, in_1[0]);
  and and_3 (blez, not_10_out, not_11_out, not_12_out, in_1[2], in_1[1], not_13_out);
  and and_4 (bgtz, not_14_out, not_15_out, not_16_out, in_1[2], in_1[1], in_1[0]);
  and and_5 (bltz, not_17_out, not_18_out, not_19_out, not_20_out, not_21_out, in_1[0]);
  and and_6 (j, not_22_out, not_23_out, not_24_out, not_25_out, in_1[1], not_26_out);
endmodule

module destinosalto (
  input  [5:0] fx,
  input  [4:0] x,
  input  [4:0] Rd,
  input  [4:0] Rt,
  input  [4:0] Rs,
  output [25:0] Output
);


  assign Output = {Rs, Rt, Rd, x, fx};
endmodule

module destinobuilder (
  input  [25:0] des,
  input  [31:0] PC,
  output [31:0] Output
);


  assign Output = {PC[31:28], des, 2'b00};
endmodule

module D_flipflop (
  input  D,
  input  clk,
  output Q,
  output noQ
);

  wire and_1_out, and_2_out, and_3_out, and_4_out, not_1_out, not_2_out, not_3_out;

  not not_1 (not_1_out, D);
  and and_1 (and_1_out, D, clk);
  and and_2 (and_2_out, clk, not_1_out);
  not not_2 (not_2_out, and_1_out);
  not not_3 (not_3_out, and_2_out);
  and and_3 (and_3_out, not_2_out, noQ);
  not not_4 (Q, and_3_out);
  and and_4 (and_4_out, Q, not_3_out);
  not not_5 (noQ, and_4_out);
endmodule

module MasterSlaveFE (
  input  in_1,
  input  in_2,
  output out_3,
  output out_4
);

  wire d_flipflop_1_q, not_1_out;

  D_flipflop d_flipflop_1 (.D(in_1), .clk(in_2), .Q(d_flipflop_1_q));  // open: noQ
  not not_1 (not_1_out, in_2);
  D_flipflop d_flipflop_2 (.D(d_flipflop_1_q), .clk(not_1_out), .Q(out_3), .noQ(out_4));
endmodule

module MasterSlaveRE (
  input  in_1,
  input  in_2,
  input  in_3,
  input  in_4,
  output out_5,
  output out_6
);

  wire and_1_out, and_2_out, d_flipflop_1_q, not_1_out, or_1_out;

  not not_1 (not_1_out, in_3);
  and and_1 (and_1_out, ~in_1, d_flipflop_1_q);  // AND_Gate
  D_flipflop d_flipflop_1 (.D(in_2), .clk(not_1_out), .Q(d_flipflop_1_q));  // open: noQ
  or or_1 (or_1_out, in_1, and_2_out);
  and and_2 (and_2_out, in_3, in_4);
  D_flipflop d_flipflop_2 (.D(and_1_out), .clk(or_1_out), .Q(out_5), .noQ(out_6));
endmodule

module myregister (
  input  [31:0] Output,
  input  L,
  input  C,
  input  clk,
  output [31:0] Output_2
);

  MasterSlaveRE masterslavere_1 (.in_2(Output[0]), .in_3(clk), .out_5(Output_2[0]), .in_1(C), .in_4(L));  // open: out_6
  MasterSlaveRE masterslavere_2 (.in_2(Output[4]), .in_3(clk), .out_5(Output_2[4]), .in_1(C), .in_4(L));  // open: out_6
  MasterSlaveRE masterslavere_3 (.in_2(Output[8]), .in_3(clk), .out_5(Output_2[8]), .in_1(C), .in_4(L));  // open: out_6
  MasterSlaveRE masterslavere_4 (
    .in_2(Output[12]), .in_3(clk), .out_5(Output_2[12]), .in_1(C), .in_4(L));  // open: out_6
  MasterSlaveRE masterslavere_5 (
    .in_2(Output[16]), .in_3(clk), .out_5(Output_2[16]), .in_1(C), .in_4(L));  // open: out_6
  MasterSlaveRE masterslavere_6 (
    .in_2(Output[20]), .in_3(clk), .out_5(Output_2[20]), .in_1(C), .in_4(L));  // open: out_6
  MasterSlaveRE masterslavere_7 (
    .in_2(Output[24]), .in_3(clk), .out_5(Output_2[24]), .in_1(C), .in_4(L));  // open: out_6
  MasterSlaveRE masterslavere_8 (
    .in_2(Output[28]), .in_3(clk), .out_5(Output_2[28]), .in_1(C), .in_4(L));  // open: out_6
  MasterSlaveRE masterslavere_9 (.in_2(Output[1]), .in_3(clk), .out_5(Output_2[1]), .in_1(C), .in_4(L));  // open: out_6
  MasterSlaveRE masterslavere_10 (
    .in_2(Output[5]), .in_3(clk), .out_5(Output_2[5]), .in_1(C), .in_4(L));  // open: out_6
  MasterSlaveRE masterslavere_11 (
    .in_2(Output[9]), .in_3(clk), .out_5(Output_2[9]), .in_1(C), .in_4(L));  // open: out_6
  MasterSlaveRE masterslavere_12 (
    .in_2(Output[13]), .in_3(clk), .out_5(Output_2[13]), .in_1(C), .in_4(L));  // open: out_6
  MasterSlaveRE masterslavere_13 (
    .in_2(Output[17]), .in_3(clk), .out_5(Output_2[17]), .in_1(C), .in_4(L));  // open: out_6
  MasterSlaveRE masterslavere_14 (
    .in_2(Output[21]), .in_3(clk), .out_5(Output_2[21]), .in_1(C), .in_4(L));  // open: out_6
  MasterSlaveRE masterslavere_15 (
    .in_2(Output[25]), .in_3(clk), .out_5(Output_2[25]), .in_1(C), .in_4(L));  // open: out_6
  MasterSlaveRE masterslavere_16 (
    .in_2(Output[29]), .in_3(clk), .out_5(Output_2[29]), .in_1(C), .in_4(L));  // open: out_6
  MasterSlaveRE masterslavere_17 (
    .in_2(Output[2]), .in_3(clk), .out_5(Output_2[2]), .in_1(C), .in_4(L));  // open: out_6
  MasterSlaveRE masterslavere_18 (
    .in_2(Output[6]), .in_3(clk), .out_5(Output_2[6]), .in_1(C), .in_4(L));  // open: out_6
  MasterSlaveRE masterslavere_19 (
    .in_2(Output[10]), .in_3(clk), .out_5(Output_2[10]), .in_1(C), .in_4(L));  // open: out_6
  MasterSlaveRE masterslavere_20 (
    .in_2(Output[14]), .in_3(clk), .out_5(Output_2[14]), .in_1(C), .in_4(L));  // open: out_6
  MasterSlaveRE masterslavere_21 (
    .in_2(Output[18]), .in_3(clk), .out_5(Output_2[18]), .in_1(C), .in_4(L));  // open: out_6
  MasterSlaveRE masterslavere_22 (
    .in_2(Output[22]), .in_3(clk), .out_5(Output_2[22]), .in_1(C), .in_4(L));  // open: out_6
  MasterSlaveRE masterslavere_23 (
    .in_2(Output[26]), .in_3(clk), .out_5(Output_2[26]), .in_1(C), .in_4(L));  // open: out_6
  MasterSlaveRE masterslavere_24 (
    .in_2(Output[30]), .in_3(clk), .out_5(Output_2[30]), .in_1(C), .in_4(L));  // open: out_6
  MasterSlaveRE masterslavere_25 (
    .in_2(Output[3]), .in_3(clk), .out_5(Output_2[3]), .in_1(C), .in_4(L));  // open: out_6
  MasterSlaveRE masterslavere_26 (
    .in_2(Output[7]), .in_3(clk), .out_5(Output_2[7]), .in_1(C), .in_4(L));  // open: out_6
  MasterSlaveRE masterslavere_27 (
    .in_2(Output[11]), .in_3(clk), .out_5(Output_2[11]), .in_1(C), .in_4(L));  // open: out_6
  MasterSlaveRE masterslavere_28 (
    .in_2(Output[15]), .in_3(clk), .out_5(Output_2[15]), .in_1(C), .in_4(L));  // open: out_6
  MasterSlaveRE masterslavere_29 (
    .in_2(Output[19]), .in_3(clk), .out_5(Output_2[19]), .in_1(C), .in_4(L));  // open: out_6
  MasterSlaveRE masterslavere_30 (
    .in_2(Output[23]), .in_3(clk), .out_5(Output_2[23]), .in_1(C), .in_4(L));  // open: out_6
  MasterSlaveRE masterslavere_31 (
    .in_2(Output[27]), .in_3(clk), .out_5(Output_2[27]), .in_1(C), .in_4(L));  // open: out_6
  MasterSlaveRE masterslavere_32 (
    .in_2(Output[31]), .in_3(clk), .out_5(Output_2[31]), .in_1(C), .in_4(L));  // open: out_6

  // Other names for the same wires on the sheet: _0 = Output[0]; _1 = Output[1]; _2 = Output[2]; _3 = Output[3];
  //   _4 = Output[4]; _5 = Output[5]; _6 = Output[6]; _7 = Output[7]; _8 = Output[8]; _9 = Output[9];
  //   _10 = Output[10]; _11 = Output[11]; _12 = Output[12]; _13 = Output[13]; _14 = Output[14]; _15 = Output[15];
  //   _16 = Output[16]; _17 = Output[17]; _18 = Output[18]; _19 = Output[19]; _20 = Output[20]; _21 = Output[21];
  //   _22 = Output[22]; _23 = Output[23]; _24 = Output[24]; _25 = Output[25]; _26 = Output[26]; _27 = Output[27];
  //   _28 = Output[28]; _29 = Output[29]; _30 = Output[30]; _31 = Output[31]; o0 = Output_2[0]; o1 = Output_2[1];
  //   o2 = Output_2[2]; o3 = Output_2[3]; o4 = Output_2[4]; o5 = Output_2[5]; o6 = Output_2[6]; o7 = Output_2[7];
  //   o8 = Output_2[8]; o9 = Output_2[9]; o10 = Output_2[10]; o11 = Output_2[11]; o12 = Output_2[12];
  //   o13 = Output_2[13]; o14 = Output_2[14]; o15 = Output_2[15]; o16 = Output_2[16]; o17 = Output_2[17];
  //   o18 = Output_2[18]; o19 = Output_2[19]; o20 = Output_2[20]; o21 = Output_2[21]; o22 = Output_2[22];
  //   o23 = Output_2[23]; o24 = Output_2[24]; o25 = Output_2[25]; o26 = Output_2[26]; o27 = Output_2[27];
  //   o28 = Output_2[28]; o29 = Output_2[29]; o30 = Output_2[30]; o31 = Output_2[31]
endmodule

module _24 (
  input  a,
  input  b,
  output q,
  output w,
  output e,
  output r
);

  wire not_1_out, not_2_out, not_3_out, not_4_out;

  and and_1 (q, a, b);
  not not_1 (not_1_out, b);
  not not_2 (not_2_out, a);
  not not_3 (not_3_out, a);
  not not_4 (not_4_out, b);
  and and_2 (w, a, not_1_out);
  and and_3 (e, not_2_out, b);
  and and_4 (r, not_3_out, not_4_out);
endmodule

module _42 (
  input  a,
  input  b,
  input  c,
  input  d,
  output a_2,
  output b_2
);

  wire and_1_out, and_2_out, and_3_out, and_4_out, not_1_out, not_2_out, not_3_out, not_4_out, not_5_out,
       not_6_out, not_7_out, not_8_out, not_9_out, not_10_out, not_11_out, not_12_out;

  not not_1 (not_1_out, a);
  not not_2 (not_2_out, c);
  not not_3 (not_3_out, d);
  not not_4 (not_4_out, b);
  not not_5 (not_5_out, c);
  not not_6 (not_6_out, d);
  not not_7 (not_7_out, a);
  not not_8 (not_8_out, b);
  not not_9 (not_9_out, d);
  not not_10 (not_10_out, b);
  not not_11 (not_11_out, c);
  not not_12 (not_12_out, d);
  and and_1 (and_1_out, not_1_out, b, not_2_out, not_3_out);
  or or_1 (a_2, and_1_out, and_2_out);
  and and_2 (and_2_out, a, not_4_out, not_5_out, not_6_out);
  and and_3 (and_3_out, not_7_out, not_8_out, c, not_9_out);
  or or_2 (b_2, and_3_out, and_4_out);
  and and_4 (and_4_out, a, not_10_out, not_11_out, not_12_out);
endmodule

module kbd (
  input  [6:0] in_1,
  output [31:0] Output
);


  assign Output = {{25{1'b0}}, in_1};
endmodule

module tty (
  input  [31:0] \input ,
  output [6:0] out_2
);


  assign out_2 = \input [6:0];
endmodule

module OPCODE111111dec (
  input  [5:0] in_1,
  output [3:0] Output
);

  wire and_1_out, and_2_out, and_3_out, and_4_out, and_5_out, and_6_out, and_7_out, not_1_out, not_2_out,
       not_3_out, not_4_out, not_5_out, not_6_out, not_7_out, not_8_out, not_9_out, not_10_out, not_11_out,
       not_12_out, not_13_out, not_14_out, not_15_out, not_16_out, not_17_out, not_18_out, not_19_out,
       not_20_out, not_21_out, not_22_out, not_23_out, not_24_out, not_25_out;

  not not_1 (not_1_out, in_1[5]);
  not not_2 (not_2_out, in_1[4]);
  not not_3 (not_3_out, in_1[3]);
  not not_4 (not_4_out, in_1[2]);
  not not_5 (not_5_out, in_1[1]);
  not not_6 (not_6_out, in_1[5]);
  not not_7 (not_7_out, in_1[4]);
  not not_8 (not_8_out, in_1[3]);
  not not_9 (not_9_out, in_1[2]);
  not not_10 (not_10_out, in_1[0]);
  not not_11 (not_11_out, in_1[5]);
  not not_12 (not_12_out, in_1[4]);
  not not_13 (not_13_out, in_1[3]);
  not not_14 (not_14_out, in_1[1]);
  not not_15 (not_15_out, in_1[0]);
  not not_16 (not_16_out, in_1[5]);
  not not_17 (not_17_out, in_1[4]);
  not not_18 (not_18_out, in_1[3]);
  not not_19 (not_19_out, in_1[2]);
  not not_20 (not_20_out, in_1[1]);
  not not_21 (not_21_out, in_1[5]);
  not not_22 (not_22_out, in_1[4]);
  not not_23 (not_23_out, in_1[3]);
  not not_24 (not_24_out, in_1[1]);
  not not_25 (not_25_out, in_1[0]);
  and and_1 (and_1_out, not_1_out, not_2_out, not_3_out, not_4_out, not_5_out, in_1[0]);
  and and_2 (and_2_out, not_6_out, not_7_out, not_8_out, not_9_out, in_1[1], not_10_out);
  and and_3 (and_3_out, not_11_out, not_12_out, not_13_out, in_1[2], not_14_out, not_15_out);
  and and_4 (and_4_out, not_16_out, not_17_out, not_18_out, not_19_out, not_20_out, in_1[0]);
  and and_5 (and_5_out, in_1[5], in_1[4], in_1[3], in_1[2], in_1[1], in_1[0]);
  and and_6 (and_6_out, not_21_out, not_22_out, not_23_out, in_1[2], not_24_out, not_25_out);
  and and_7 (and_7_out, in_1[5], in_1[4], in_1[3], in_1[2], in_1[1], in_1[0]);
  or or_1 (Output[2], and_1_out, and_2_out, and_3_out);
  or or_2 (Output[1], and_4_out, and_5_out);
  or or_3 (Output[0], and_6_out, and_7_out);

  assign Output[3] = 1'b0;
endmodule

module writewith11 (
  input  [1:0] OP,
  input  [3:0] ARIT,
  output write,
  output halt,
  output tty,
  output kbd,
  output rnd
);

  wire not_1_out, not_2_out, not_3_out, not_4_out, not_5_out, not_6_out, not_7_out, not_8_out, not_9_out,
       not_10_out, not_11_out;

  not not_1 (not_1_out, ARIT[3]);
  not not_2 (not_2_out, ARIT[1]);
  not not_3 (not_3_out, ARIT[3]);
  not not_4 (not_4_out, ARIT[2]);
  not not_5 (not_5_out, ARIT[3]);
  not not_6 (not_6_out, ARIT[0]);
  not not_7 (not_7_out, ARIT[3]);
  not not_8 (not_8_out, ARIT[1]);
  not not_9 (not_9_out, ARIT[3]);
  not not_10 (not_10_out, ARIT[1]);
  not not_11 (not_11_out, ARIT[0]);
  and and_1 (write, OP[1], OP[0], not_1_out, ARIT[2], not_2_out);
  and and_2 (halt, OP[1], OP[0], not_3_out, not_4_out, ARIT[1], ARIT[0]);
  and and_3 (tty, OP[1], OP[0], not_5_out, ARIT[2], ARIT[1], not_6_out);
  and and_4 (kbd, OP[1], OP[0], not_7_out, ARIT[2], not_8_out, ARIT[0]);
  and and_5 (rnd, OP[1], OP[0], not_9_out, ARIT[2], not_10_out, not_11_out);
endmodule

module lwsw (
  input  [5:0] in_1,
  output lw,
  output sw
);

  wire not_1_out, not_2_out, not_3_out, not_4_out, not_5_out;

  not not_1 (not_1_out, in_1[4]);
  not not_2 (not_2_out, in_1[3]);
  not not_3 (not_3_out, in_1[2]);
  not not_4 (not_4_out, in_1[4]);
  not not_5 (not_5_out, in_1[2]);
  and and_1 (lw, in_1[5], not_1_out, not_2_out, not_3_out, in_1[1], in_1[0]);
  and and_2 (sw, in_1[5], not_4_out, in_1[3], not_5_out, in_1[1], in_1[0]);
endmodule

module awaitersi (
  input  start,
  input  [3:0] \time ,
  input  clk,
  output \end 
);

  wire comparator_1_gt, or_1_out;
  wire [3:0] counter_1_q;

  or or_1 (or_1_out, start, comparator_1_gt);
  Counter #(.width(4), .max('hf), .ongoal("stay")) counter_1 (
    .load(or_1_out), .D(\time ), .count(comparator_1_gt), .Q(counter_1_q), .clk(clk));  // open: carry, clr
  Comparator #(.width(4), .mode("unsigned")) comparator_1 (
    .a(counter_1_q), .b(4'b0000), .gt(comparator_1_gt), .eq(\end ));  // open: lt
endmodule

module DIVs (
  input  [31:0] A,
  input  [31:0] B,
  output [31:0] out,
  output [31:0] rest
);

  wire xor_1_out;
  wire [31:0] divider_1_out, divider_1_rem, multiplexer_1_out, multiplexer_2_out, negator_1_out,
       negator_2_out, negator_3_out, negator_4_out;

  // Probe on B
  // Probe on A
  Multiplexer #(.width(32), .enable("false")) multiplexer_1 (
    .in0(A), .in1(negator_1_out), .out(multiplexer_1_out), .sel(A[31]));
  Negator #(.width(32)) negator_1 (.in(A), .out(negator_1_out));
  Multiplexer #(.width(32), .enable("false")) multiplexer_2 (
    .in0(B), .in1(negator_2_out), .out(multiplexer_2_out), .sel(B[31]));
  Negator #(.width(32)) negator_2 (.in(B), .out(negator_2_out));
  Divider #(.width(32)) divider_1 (
    .a(multiplexer_1_out), .b(multiplexer_2_out), .out(divider_1_out), .rem(divider_1_rem));  // open: upper
  xor xor_1 (xor_1_out, A[31], B[31]);
  Negator #(.width(32)) negator_3 (.in(divider_1_out), .out(negator_3_out));
  Multiplexer #(.width(32), .enable("false")) multiplexer_3 (
    .in0(divider_1_rem), .in1(negator_4_out), .out(rest), .sel(xor_1_out));
  Negator #(.width(32)) negator_4 (.in(divider_1_rem), .out(negator_4_out));
  // Probe on out
  Multiplexer #(.width(32), .enable("false")) multiplexer_4 (
    .in0(divider_1_out), .in1(negator_3_out), .out(out), .sel(xor_1_out));
  // Probe on rest
endmodule

module MULTs (
  input  [31:0] in_1,
  input  [31:0] B,
  output [31:0] Output,
  output [31:0] Output_2
);

  wire [31:0] adder_1_out, multiplexer_1_out, multiplexer_2_out, multiplier_1_cout;

  // Probe on in_1
  // Probe on B
  // Probe on Output
  Multiplexer #(.width(32), .enable("false")) multiplexer_1 (
    .in0({32{1'b0}}), .in1(in_1), .out(multiplexer_1_out), .sel(B[31]));
  Multiplexer #(.width(32), .enable("false")) multiplexer_2 (
    .in0({32{1'b0}}), .in1(B), .out(multiplexer_2_out), .sel(in_1[31]));
  Multiplier #(.width(32)) multiplier_1 (.a(in_1), .b(B), .out(Output), .cout(multiplier_1_cout));  // open: cin
  Adder #(.width(32)) adder_1 (.a(multiplexer_1_out), .b(multiplexer_2_out), .out(adder_1_out));  // open: cin, cout
  // Probe on Output_2
  Adder #(.width(32)) adder_2 (.a(multiplier_1_cout), .b(adder_1_out), .out(Output_2));  // open: cin, cout

  // Other names for the same wires on the sheet: A[31:0] = in_1
endmodule

module tests (
  input  [31:0] in_1,
  input  in_2,
  input  [5:0] in_3,
  input  [31:0] in_4,
  input  [31:0] Output,
  input  in_6,
  input  in_7,
  input  in_8,
  input  in_9,
  input  in_10,
  input  in_11,
  input  in_12,
  input  in_13,
  input  in_14,
  input  in_15,
  input  in_16,
  input  in_17,
  input  in_18,
  input  in_19,
  input  [3:0] in_20,
  input  in_21,
  input  in_22,
  input  [31:0] in_23,
  input  [31:0] in_24,
  input  [31:0] a,
  input  [31:0] b,
  input  in_27,
  input  [2:0] in_28,
  input  [31:0] b_2,
  input  [4:0] in_30,
  input  [1:0] in_31,
  output [31:0] Output_2,
  output Output_3,
  output [31:0] Output_4,
  output [4:0] Output_5,
  output [31:0] Output_6,
  output [31:0] Output_7,
  output out_38,
  output out_39,
  output out_40,
  output out_41,
  output out_42,
  output out_43,
  output [31:0] out_44,
  output Output_8
);

  wire and_1_out, clock_1_out, clock_2_out, clock_3_out, clock_4_out, clock_5_out, n24_1_e, n24_1_q, n24_1_r,
       n24_1_w, n42_1_a_2, n42_1_b_2;
  wire [31:0] big_to_low_1_output, mihi, milo, suhi, sulo;

  Subtractor #(.width(32)) subtractor_1 (.a(in_1), .b(32'h4), .out(Output_2));  // open: bin, bout
  _24 u_24_1 (.a(in_13), .b(in_15), .q(n24_1_q), .w(n24_1_w), .e(n24_1_e), .r(n24_1_r));
  _42 u_42_1 (.a(in_17), .b(in_18), .c(in_19), .d(in_21), .a_2(n42_1_a_2), .b_2(n42_1_b_2));
  BitSelector #(.width(32)) bitselector_1 (.in(b_2), .out(Output_8), .sel(in_30));
  _42 u_42_2 (.a(n24_1_q), .b(n24_1_w), .c(n24_1_e), .d(n24_1_r), .a_2(out_38), .b_2(out_39));
  _24 u_24_2 (.a(n42_1_a_2), .b(n42_1_b_2), .q(out_40), .w(out_41), .e(out_42), .r(out_43));
  MULTs mults_1 (.in_1(in_24), .B(b), .Output(milo), .Output_2(mihi));
  Multiplier #(.width(32)) multiplier_1 (.a(in_24), .b(b), .out(sulo), .cout(suhi));  // open: cin
  Clock clock_1 (.out(clock_1_out));
  myregister myregister_1 (.Output(in_4), .L(in_6), .C(in_8), .clk(in_7), .Output_2(Output_6));
  Decoder #(.select(2), .enable("false")) decoder_1 (.sel(in_31));  // open: out0, out1, out2, out3
  RAM_part #(.addrWidth(6), .dataWidth(5), .bus("separate")) ram_1 ();  // open: addr, din, data, str, sel, clk, ld, clr
  Random #(.width(1)) random_1 (.clk(clock_1_out), .next(clock_1_out), .out(Output_3));  // open: clr
  Register #(.width(32)) register_1 ();  // open: D, en, Q, clk, clr
  Random #(.width(3)) random_2 (.clk(in_11), .next(in_11));  // open: out, clr
  Random #(.width(3)) random_3 (.clk(in_11), .next(in_11));  // open: out, clr
  Random #(.width(3)) random_4 (.clk(in_11), .next(in_11));  // open: out, clr
  Random #(.width(3)) random_5 (.clk(in_11), .next(in_11));  // open: out, clr
  Random #(.width(3)) random_6 (.clk(in_11), .next(in_11));  // open: out, clr
  // Probe on in_24
  RAM_part #(.addrWidth(6), .dataWidth(16), .bus("separate")) ram_2 ();  // open: addr, din, data, str, sel, clk, ld, clr
  Clock clock_2 (.out(clock_2_out));
  Clock clock_3 (.out(clock_3_out));
  // Probe on b
  Priority_Encoder priority_encoder_1 (.out(in_28));  // open: in0, in1, in2, in3, in4, in5, in6, in7, en_in
  Random #(.width(32)) random_7 (.clk(clock_2_out), .next(in_2), .out(Output_4));  // open: clr
  and and_1 (and_1_out, clock_3_out, in_12);
  Register #(.width(4)) register_2 (.D(in_20), .en(in_22), .clk(clock_4_out));  // open: Q, clr
  Clock clock_4 (.out(clock_4_out));
  RAM_part #(.addrWidth(6), .dataWidth(32), .bus("separate")) ram_3 ();  // open: addr, din, data, str, sel, clk, ld, clr
  Clock clock_5 (.out(clock_5_out));
  big_to_low big_to_low_1 (.in_1(in_23), .Output(big_to_low_1_output));
  big_to_low big_to_low_2 (.in_1(big_to_low_1_output), .Output(out_44));
  // Probe on milo
  // Probe on sulo
  RAM_part #(.addrWidth(6), .dataWidth(32), .bus("separate")) ram_4 (
    .addr(in_3), .din(Output), .data(Output_7), .sel(in_9), .clk(clock_5_out), .ld(in_10));  // open: str, clr
  Random random_8 (.clk(and_1_out), .next(in_16), .clr(in_14));  // open: out
  Random random_9 (.clk(and_1_out), .next(in_16), .clr(in_14));  // open: out
  // Probe on mihi
  // Probe on suhi
  RAM_part #(.addrWidth(6), .dataWidth(32), .bus("separate")) ram_5 ();  // open: addr, din, data, str, sel, clk, ld, clr
  RAM_part #(.addrWidth(6), .dataWidth(32), .bus("separate")) ram_6 ();  // open: addr, din, data, str, sel, clk, ld, clr

  assign Output_5 = {5{1'b1}};

  // Other names for the same wires on the sheet: a_t[31:0] = in_24; set = in_11
endmodule

module ControlUnitObsolete (
  input  init,
  input  start,
  input  halt,
  input  restart,
  input  clk,
  input  [3:0] RAMReadT,
  input  [3:0] RAMWriteT,
  input  RAM,
  input  R0_W1,
  output Readitnow,
  output globalclock
);

  wire awaiter_1_end, clock_1_out, d_ff_1_q, d_ff_2_q, d_ff_3_q, demultiplexer_1_out0, demultiplexer_1_out1,
       demultiplexer_2_out0, demultiplexer_2_out1, demultiplexer_3_out0, or_1_out, or_2_out, or_3_out;
  wire [3:0] multiplexer_1_out;

  or or_1 (or_1_out, demultiplexer_1_out0, demultiplexer_2_out1, init);
  Clock clock_1 (.out(clock_1_out));
  D_Flip_Flop #(.trigger("falling")) d_ff_1 (
    .clk(globalclock), .D(or_1_out), .Q(d_ff_1_q));  // open: Qn, preset, en, reset
  Demultiplexer #(.enable("false")) demultiplexer_1 (
    .out0(demultiplexer_1_out0), .out1(demultiplexer_1_out1), .in(d_ff_1_q), .sel(start));
  or or_2 (or_2_out, demultiplexer_2_out0, demultiplexer_1_out1);
  D_Flip_Flop #(.trigger("falling")) d_ff_2 (
    .clk(globalclock), .D(or_2_out), .Q(d_ff_2_q));  // open: Qn, preset, en, reset
  Demultiplexer #(.enable("false")) demultiplexer_2 (
    .out0(demultiplexer_2_out0), .out1(demultiplexer_2_out1), .in(d_ff_2_q), .sel(halt));
  Multiplexer #(.width(4), .enable("false")) multiplexer_1 (
    .in0(RAMReadT), .in1(RAMWriteT), .out(multiplexer_1_out), .sel(R0_W1));
  awaiter awaiter_1 (.in_2(multiplexer_1_out), .\end (awaiter_1_end), .start(RAM), .clk(clk), .\do (Readitnow));
  D_Flip_Flop #(.trigger("falling")) d_ff_3 (
    .clk(globalclock), .D(or_3_out), .Q(d_ff_3_q));  // open: Qn, preset, en, reset
  buf or_3 (or_3_out, demultiplexer_3_out0);  // OR_Gate
  and and_1 (globalclock, awaiter_1_end, clk);
  Demultiplexer #(.enable("false")) demultiplexer_3 (
    .out0(demultiplexer_3_out0), .in(d_ff_3_q), .sel(restart));  // open: out1

  // Other names for the same wires on the sheet: gclk = globalclock; RT[3:0] = RAMReadT; WT[3:0] = RAMWriteT

  // Notes on the sheet:
  //   IDLE
  //   WHILE
  //   END
endmodule

module writealucountingsw (
  input  [3:0] ARIT,
  input  sw,
  output write00n01
);

  wire and_1_out, and_2_out, and_3_out, and_4_out, and_5_out, not_1_out, not_2_out, not_3_out, not_4_out,
       not_5_out, not_6_out, not_7_out, not_8_out, not_9_out, not_10_out, not_11_out;

  not not_1 (not_1_out, ARIT[2]);
  not not_2 (not_2_out, ARIT[1]);
  not not_3 (not_3_out, sw);
  not not_4 (not_4_out, ARIT[2]);
  not not_5 (not_5_out, ARIT[0]);
  not not_6 (not_6_out, sw);
  not not_7 (not_7_out, sw);
  and and_1 (and_1_out, not_1_out, not_2_out, ARIT[0], not_3_out);
  and and_2 (and_2_out, not_4_out, ARIT[1], not_5_out, not_6_out);
  and and_3 (and_3_out, ARIT[2], ARIT[1], ARIT[0], not_7_out);
  not not_8 (not_8_out, ARIT[2]);
  and and_4 (and_4_out, ARIT[3], not_8_out, not_9_out);
  not not_9 (not_9_out, sw);
  not not_10 (not_10_out, ARIT[0]);
  and and_5 (and_5_out, ARIT[3], not_10_out, not_11_out);
  not not_11 (not_11_out, sw);
  or or_1 (write00n01, and_1_out, and_2_out, and_3_out, and_4_out, and_5_out);
endmodule

module useCTE (
  input  [1:0] in_1,
  input  beq,
  input  bne,
  output cte
);

  wire not_1_out, not_2_out, not_3_out;

  not not_1 (not_1_out, in_1[1]);
  not not_2 (not_2_out, beq);
  not not_3 (not_3_out, bne);
  and and_1 (cte, not_1_out, in_1[0], not_2_out, not_3_out);
endmodule

module big_to_low (
  input  [31:0] in_1,
  output [31:0] Output
);


  assign Output = {in_1[7:0], in_1[15:8], in_1[23:16], in_1[31:24]};
endmodule

module addrnmask (
  input  [31:0] in_1,
  output [3:0] mask,
  output [1:0] masksel,
  output [15:0] addr
);

  Demultiplexer #(.select(2), .enable("false")) demultiplexer_1 (
    .out0(mask[0]), .out1(mask[1]), .out2(mask[2]), .out3(mask[3]), .in(1'b1), .sel(in_1[3:2]));

  assign addr = in_1[19:4];
  assign masksel = in_1[3:2];
endmodule

module mask (
  input  a,
  input  b,
  output a_2,
  output b_2,
  output c,
  output d
);

  wire not_1_out, not_2_out, not_3_out, not_4_out;

  and and_1 (a_2, a, b);
  not not_1 (not_1_out, b);
  not not_2 (not_2_out, a);
  not not_3 (not_3_out, a);
  not not_4 (not_4_out, b);
  and and_2 (b_2, a, not_1_out);
  and and_3 (c, not_2_out, b);
  and and_4 (d, not_3_out, not_4_out);
endmodule

module cutrash (
  output tapRAM,
  output Write
);

  wire and_1_out, and_2_out, and_3_out, and_4_out, callI, callR, clk, d_ff_1_q, d_ff_2_q, d_ff_3_q, d_ff_4_q,
       demultiplexer_1_out1, demultiplexer_2_out0, demultiplexer_3_out1, DO, frmrst, halt, inst, loaded,
       LoadI, not_1_out, or_2_out, or_3_out, or_4_out, or_6_out, or_7_out, or_10_out, R0_W1, RAM, rst, run,
       run1, run2, tapRAM_t, tohalt, undriven, undriven_2, undriven_3, undriven_4, waitin1, waitin2, WriteTap;
  wire [3:0] multiplexer_1_out, RT, WT;
  wire [7:0] counter_1_q;
  wire [31:0] counter_2_q;

  or or_1 (callI, rst, inst);
  D_Flip_Flop #(.trigger("falling")) d_ff_1 (
    .clk(clk), .D(demultiplexer_1_out1), .Q(d_ff_1_q), .preset(rst), .en(1'b1));  // open: Qn, reset
  Demultiplexer #(.enable("false")) demultiplexer_1 (
    .out0(frmrst), .out1(demultiplexer_1_out1), .in(d_ff_1_q), .sel(rst));
  or or_2 (or_2_out, callI, waitin1);
  Demultiplexer #(.enable("false")) demultiplexer_2 (
    .out0(demultiplexer_2_out0), .out1(tohalt), .in(d_ff_2_q), .sel(halt));
  D_Flip_Flop #(.trigger("falling")) d_ff_2 (
    .clk(clk), .D(undriven), .Q(d_ff_2_q), .reset(rst));  // open: Qn, preset, en
  or or_3 (or_3_out, callR, waitin2);
  D_Flip_Flop #(.trigger("falling")) d_ff_3 (
    .clk(clk), .D(or_2_out), .Q(d_ff_3_q), .preset(rst));  // open: Qn, en, reset
  D_Flip_Flop #(.trigger("falling")) d_ff_4 (
    .clk(clk), .D(or_3_out), .Q(d_ff_4_q), .reset(rst));  // open: Qn, preset, en
  Demultiplexer #(.enable("false")) demultiplexer_3 (
    .out0(waitin1), .out1(demultiplexer_3_out1), .in(d_ff_3_q), .sel(loaded));
  Demultiplexer #(.enable("false")) demultiplexer_4 (.out0(run1), .out1(callR), .in(demultiplexer_2_out0), .sel(RAM));
  Demultiplexer #(.enable("false")) demultiplexer_5 (.out0(waitin2), .out1(run2), .in(d_ff_4_q), .sel(loaded));
  D_Flip_Flop #(.trigger("falling")) d_ff_5 (.clk(clk), .D(run), .Q(inst), .reset(rst));  // open: Qn, preset, en
  and and_1 (and_1_out, DO, RAM);
  and and_2 (and_2_out, ~callI, R0_W1);  // AND_Gate
  or or_4 (or_4_out, waitin1, waitin2);
  // OR_Gate or_5 has open pins: in0=LoadI, in1=waitin1, out=open
  and and_3 (and_3_out, callI, ~undriven_4);  // AND_Gate
  or or_6 (or_6_out, and_3_out, and_4_out);
  Multiplexer #(.width(4), .enable("false")) multiplexer_1 (
    .in0(RT), .in1(WT), .out(multiplexer_1_out), .sel(and_2_out));
  or or_7 (or_7_out, LoadI, or_4_out);
  // OR_Gate or_8 has open pins: in0=undriven_2, in1=or_7_out, in2=undriven_3, out=open
  and and_4 (and_4_out, ~undriven_4, callR);  // AND_Gate
  awaitersi awaitersi_1 (.\time (multiplexer_1_out), .\end (loaded), .start(or_6_out), .clk(clk));
  or or_9 (run, run1, run2);
  // Probe on counter_1_q
  Counter counter_1 (.count(or_4_out), .Q(counter_1_q), .clk(clk), .clr(or_10_out));  // open: load, D, carry
  or or_10 (or_10_out, not_1_out, rst);
  not not_1 (not_1_out, or_4_out);
  Counter #(.width(32), .max('hffffffff)) counter_2 (
    .count(clk), .Q(counter_2_q), .clk(clk), .clr(rst));  // open: load, D, carry
  and and_5 (WriteTap, ~callI, R0_W1);  // AND_Gate
  or or_11 (tapRAM_t, callI, callR);
  // Probe on counter_2_q

  // Other names for the same wires on the sheet: callinstin = callI; loadRAM = callR
endmodule

module efficiencecount (
  input  rst,
  input  clock,
  input  stop,
  output [31:0] Output
);

  wire and_1_out;

  and and_1 (and_1_out, clock, ~stop);  // AND_Gate
  Counter #(.width(32), .max('hffffffff)) counter_1 (
    .count(1'b1), .Q(Output), .clk(and_1_out), .clr(rst));  // open: load, D, carry
endmodule

module adrrtoselntag (
  input  [15:0] addr,
  output [4:0] selector,
  output [10:0] tag
);


  assign selector = addr[4:0];
  assign tag = {addr[15:6], 1'b1};
endmodule

module CacheBank32 (
  input  [31:0] D,
  input  c,
  input  r,
  input  RW,
  input  [4:0] LS,
  output [31:0] OUTPUT
);

  wire l0, l1, l2, l3, l4, l5, l6, l7, l8, l9, l10, l11, l12, l13, l14, l15, l16, l17, l18, l19, l20, l21,
       l22, l23, l24, l25, l26, l27, l28, l29, l30, l31;
  wire [31:0] r0, r1, r2, r3, r4, r5, r6, r7, r8, r9, r10, r11, r12, r13, r14, r15, r16, r17, r18, r19, r20,
       r21, r22, r23, r24, r25, r26, r27, r28, r29, r30, r31;

  Register #(.width(32), .trigger("falling")) register_1 (.D(D), .en(l0), .Q(r0), .clk(c), .clr(r));
  Register #(.width(32), .trigger("falling")) register_2 (.D(D), .en(l8), .Q(r8), .clk(c), .clr(r));
  Register #(.width(32), .trigger("falling")) register_3 (.D(D), .en(l16), .Q(r16), .clk(c), .clr(r));
  Register #(.width(32), .trigger("falling")) register_4 (.D(D), .en(l24), .Q(r24), .clk(c), .clr(r));
  Demultiplexer #(.select(5), .disabled(0)) demultiplexer_1 (
    .out0(l0), .out1(l1), .out2(l2), .out3(l3), .out4(l4), .out5(l5), .out6(l6), .out7(l7), .out8(l8),
    .out9(l9), .out10(l10), .out11(l11), .out12(l12), .out13(l13), .out14(l14), .out15(l15), .out16(l16),
    .out17(l17), .out18(l18), .out19(l19), .out20(l20), .out21(l21), .out22(l22), .out23(l23), .out24(l24),
    .out25(l25), .out26(l26), .out27(l27), .out28(l28), .out29(l29), .out30(l30), .out31(l31), .in(1'b1),
    .sel(LS), .en(RW));
  Register #(.width(32), .trigger("falling")) register_5 (.D(D), .en(l1), .Q(r1), .clk(c), .clr(r));
  Register #(.width(32), .trigger("falling")) register_6 (.D(D), .en(l9), .Q(r9), .clk(c), .clr(r));
  Register #(.width(32), .trigger("falling")) register_7 (.D(D), .en(l17), .Q(r17), .clk(c), .clr(r));
  Register #(.width(32), .trigger("falling")) register_8 (.D(D), .en(l25), .Q(r25), .clk(c), .clr(r));
  Register #(.width(32), .trigger("falling")) register_9 (.D(D), .en(l2), .Q(r2), .clk(c), .clr(r));
  Register #(.width(32), .trigger("falling")) register_10 (.D(D), .en(l10), .Q(r10), .clk(c), .clr(r));
  Register #(.width(32), .trigger("falling")) register_11 (.D(D), .en(l18), .Q(r18), .clk(c), .clr(r));
  Register #(.width(32), .trigger("falling")) register_12 (.D(D), .en(l26), .Q(r26), .clk(c), .clr(r));
  Register #(.width(32), .trigger("falling")) register_13 (.D(D), .en(l3), .Q(r3), .clk(c), .clr(r));
  Register #(.width(32), .trigger("falling")) register_14 (.D(D), .en(l11), .Q(r11), .clk(c), .clr(r));
  Register #(.width(32), .trigger("falling")) register_15 (.D(D), .en(l19), .Q(r19), .clk(c), .clr(r));
  Register #(.width(32), .trigger("falling")) register_16 (.D(D), .en(l27), .Q(r27), .clk(c), .clr(r));
  Multiplexer #(.select(5), .width(32), .enable("false")) multiplexer_1 (
    .in0(r0), .in1(r1), .in2(r2), .in3(r3), .in4(r4), .in5(r5), .in6(r6), .in7(r7), .in8(r8), .in9(r9),
    .in10(r10), .in11(r11), .in12(r12), .in13(r13), .in14(r14), .in15(r15), .in16(r16), .in17(r17),
    .in18(r18), .in19(r19), .in20(r20), .in21(r21), .in22(r22), .in23(r23), .in24(r24), .in25(r25),
    .in26(r26), .in27(r27), .in28(r28), .in29(r29), .in30(r30), .in31(r31), .out(OUTPUT), .sel(LS));
  Register #(.width(32), .trigger("falling")) register_17 (.D(D), .en(l4), .Q(r4), .clk(c), .clr(r));
  Register #(.width(32), .trigger("falling")) register_18 (.D(D), .en(l12), .Q(r12), .clk(c), .clr(r));
  Register #(.width(32), .trigger("falling")) register_19 (.D(D), .en(l20), .Q(r20), .clk(c), .clr(r));
  Register #(.width(32), .trigger("falling")) register_20 (.D(D), .en(l28), .Q(r28), .clk(c), .clr(r));
  Register #(.width(32), .trigger("falling")) register_21 (.D(D), .en(l5), .Q(r5), .clk(c), .clr(r));
  Register #(.width(32), .trigger("falling")) register_22 (.D(D), .en(l13), .Q(r13), .clk(c), .clr(r));
  Register #(.width(32), .trigger("falling")) register_23 (.D(D), .en(l21), .Q(r21), .clk(c), .clr(r));
  Register #(.width(32), .trigger("falling")) register_24 (.D(D), .en(l29), .Q(r29), .clk(c), .clr(r));
  Register #(.width(32), .trigger("falling")) register_25 (.D(D), .en(l6), .Q(r6), .clk(c), .clr(r));
  Register #(.width(32), .trigger("falling")) register_26 (.D(D), .en(l14), .Q(r14), .clk(c), .clr(r));
  Register #(.width(32), .trigger("falling")) register_27 (.D(D), .en(l22), .Q(r22), .clk(c), .clr(r));
  Register #(.width(32), .trigger("falling")) register_28 (.D(D), .en(l30), .Q(r30), .clk(c), .clr(r));
  Register #(.width(32), .trigger("falling")) register_29 (.D(D), .en(l7), .Q(r7), .clk(c), .clr(r));
  Register #(.width(32), .trigger("falling")) register_30 (.D(D), .en(l15), .Q(r15), .clk(c), .clr(r));
  Register #(.width(32), .trigger("falling")) register_31 (.D(D), .en(l23), .Q(r23), .clk(c), .clr(r));
  Register #(.width(32), .trigger("falling")) register_32 (.D(D), .en(l31), .Q(r31), .clk(c), .clr(r));

  // Other names for the same wires on the sheet: di[31:0] = D
endmodule

module CacheBank11 (
  input  [10:0] D,
  input  c,
  input  r,
  input  RW,
  input  [4:0] LS,
  output [10:0] OUTPUT
);

  wire l0, l1, l2, l3, l4, l5, l6, l7, l8, l9, l10, l11, l12, l13, l14, l15, l16, l17, l18, l19, l20, l21,
       l22, l23, l24, l25, l26, l27, l28, l29, l30, l31;
  wire [10:0] r0, r1, r2, r3, r4, r5, r6, r7, r8, r9, r10, r11, r12, r13, r14, r15, r16, r17, r18, r19, r20,
       r21, r22, r23, r24, r25, r26, r27, r28, r29, r30, r31;

  Register #(.width(11), .trigger("falling")) register_1 (.D(D), .en(l0), .Q(r0), .clk(c), .clr(r));
  Register #(.width(11), .trigger("falling")) register_2 (.D(D), .en(l8), .Q(r8), .clk(c), .clr(r));
  Register #(.width(11), .trigger("falling")) register_3 (.D(D), .en(l16), .Q(r16), .clk(c), .clr(r));
  Register #(.width(11), .trigger("falling")) register_4 (.D(D), .en(l24), .Q(r24), .clk(c), .clr(r));
  Demultiplexer #(.select(5), .disabled(0)) demultiplexer_1 (
    .out0(l0), .out1(l1), .out2(l2), .out3(l3), .out4(l4), .out5(l5), .out6(l6), .out7(l7), .out8(l8),
    .out9(l9), .out10(l10), .out11(l11), .out12(l12), .out13(l13), .out14(l14), .out15(l15), .out16(l16),
    .out17(l17), .out18(l18), .out19(l19), .out20(l20), .out21(l21), .out22(l22), .out23(l23), .out24(l24),
    .out25(l25), .out26(l26), .out27(l27), .out28(l28), .out29(l29), .out30(l30), .out31(l31), .in(1'b1),
    .sel(LS), .en(RW));
  Register #(.width(11), .trigger("falling")) register_5 (.D(D), .en(l1), .Q(r1), .clk(c), .clr(r));
  Register #(.width(11), .trigger("falling")) register_6 (.D(D), .en(l9), .Q(r9), .clk(c), .clr(r));
  Register #(.width(11), .trigger("falling")) register_7 (.D(D), .en(l17), .Q(r17), .clk(c), .clr(r));
  Register #(.width(11), .trigger("falling")) register_8 (.D(D), .en(l25), .Q(r25), .clk(c), .clr(r));
  Register #(.width(11), .trigger("falling")) register_9 (.D(D), .en(l2), .Q(r2), .clk(c), .clr(r));
  Register #(.width(11), .trigger("falling")) register_10 (.D(D), .en(l10), .Q(r10), .clk(c), .clr(r));
  Register #(.width(11), .trigger("falling")) register_11 (.D(D), .en(l18), .Q(r18), .clk(c), .clr(r));
  Register #(.width(11), .trigger("falling")) register_12 (.D(D), .en(l26), .Q(r26), .clk(c), .clr(r));
  Register #(.width(11), .trigger("falling")) register_13 (.D(D), .en(l3), .Q(r3), .clk(c), .clr(r));
  Register #(.width(11), .trigger("falling")) register_14 (.D(D), .en(l11), .Q(r11), .clk(c), .clr(r));
  Register #(.width(11), .trigger("falling")) register_15 (.D(D), .en(l19), .Q(r19), .clk(c), .clr(r));
  Register #(.width(11), .trigger("falling")) register_16 (.D(D), .en(l27), .Q(r27), .clk(c), .clr(r));
  Multiplexer #(.select(5), .width(11), .enable("false")) multiplexer_1 (
    .in0(r0), .in1(r1), .in2(r2), .in3(r3), .in4(r4), .in5(r5), .in6(r6), .in7(r7), .in8(r8), .in9(r9),
    .in10(r10), .in11(r11), .in12(r12), .in13(r13), .in14(r14), .in15(r15), .in16(r16), .in17(r17),
    .in18(r18), .in19(r19), .in20(r20), .in21(r21), .in22(r22), .in23(r23), .in24(r24), .in25(r25),
    .in26(r26), .in27(r27), .in28(r28), .in29(r29), .in30(r30), .in31(r31), .out(OUTPUT), .sel(LS));
  Register #(.width(11), .trigger("falling")) register_17 (.D(D), .en(l4), .Q(r4), .clk(c), .clr(r));
  Register #(.width(11), .trigger("falling")) register_18 (.D(D), .en(l12), .Q(r12), .clk(c), .clr(r));
  Register #(.width(11), .trigger("falling")) register_19 (.D(D), .en(l20), .Q(r20), .clk(c), .clr(r));
  Register #(.width(11), .trigger("falling")) register_20 (.D(D), .en(l28), .Q(r28), .clk(c), .clr(r));
  Register #(.width(11), .trigger("falling")) register_21 (.D(D), .en(l5), .Q(r5), .clk(c), .clr(r));
  Register #(.width(11), .trigger("falling")) register_22 (.D(D), .en(l13), .Q(r13), .clk(c), .clr(r));
  Register #(.width(11), .trigger("falling")) register_23 (.D(D), .en(l21), .Q(r21), .clk(c), .clr(r));
  Register #(.width(11), .trigger("falling")) register_24 (.D(D), .en(l29), .Q(r29), .clk(c), .clr(r));
  Register #(.width(11), .trigger("falling")) register_25 (.D(D), .en(l6), .Q(r6), .clk(c), .clr(r));
  Register #(.width(11), .trigger("falling")) register_26 (.D(D), .en(l14), .Q(r14), .clk(c), .clr(r));
  Register #(.width(11), .trigger("falling")) register_27 (.D(D), .en(l22), .Q(r22), .clk(c), .clr(r));
  Register #(.width(11), .trigger("falling")) register_28 (.D(D), .en(l30), .Q(r30), .clk(c), .clr(r));
  Register #(.width(11), .trigger("falling")) register_29 (.D(D), .en(l7), .Q(r7), .clk(c), .clr(r));
  Register #(.width(11), .trigger("falling")) register_30 (.D(D), .en(l15), .Q(r15), .clk(c), .clr(r));
  Register #(.width(11), .trigger("falling")) register_31 (.D(D), .en(l23), .Q(r23), .clk(c), .clr(r));
  Register #(.width(11), .trigger("falling")) register_32 (.D(D), .en(l31), .Q(r31), .clk(c), .clr(r));

  // Other names for the same wires on the sheet: di[10:0] = D
endmodule
module CacheBank1 (
  input  D,
  input  c,
  input  r,
  input  RW,
  input  [4:0] LS,
  output OUTPUT
);

  wire l0, l1, l2, l3, l4, l5, l6, l7, l8, l9, l10, l11, l12, l13, l14, l15, l16, l17, l18, l19, l20, l21,
       l22, l23, l24, l25, l26, l27, l28, l29, l30, l31, r0, r1, r2, r3, r4, r5, r6, r7, r8, r9, r10, r11,
       r12, r13, r14, r15, r16, r17, r18, r19, r20, r21, r22, r23, r24, r25, r26, r27, r28, r29, r30, r31;

  Register #(.width(1), .trigger("falling")) register_1 (.D(RW), .en(l0), .Q(r0), .clk(c), .clr(r));
  Register #(.width(1), .trigger("falling")) register_2 (.D(RW), .en(l8), .Q(r8), .clk(c), .clr(r));
  Register #(.width(1), .trigger("falling")) register_3 (.D(RW), .en(l16), .Q(r16), .clk(c), .clr(r));
  Register #(.width(1), .trigger("falling")) register_4 (.D(RW), .en(l24), .Q(r24), .clk(c), .clr(r));
  Demultiplexer #(.select(5), .disabled(0)) demultiplexer_1 (
    .out0(l0), .out1(l1), .out2(l2), .out3(l3), .out4(l4), .out5(l5), .out6(l6), .out7(l7), .out8(l8),
    .out9(l9), .out10(l10), .out11(l11), .out12(l12), .out13(l13), .out14(l14), .out15(l15), .out16(l16),
    .out17(l17), .out18(l18), .out19(l19), .out20(l20), .out21(l21), .out22(l22), .out23(l23), .out24(l24),
    .out25(l25), .out26(l26), .out27(l27), .out28(l28), .out29(l29), .out30(l30), .out31(l31), .in(1'b1),
    .sel(LS), .en(RW));
  Register #(.width(1), .trigger("falling")) register_5 (.D(RW), .en(l1), .Q(r1), .clk(c), .clr(r));
  Register #(.width(1), .trigger("falling")) register_6 (.D(RW), .en(l9), .Q(r9), .clk(c), .clr(r));
  Register #(.width(1), .trigger("falling")) register_7 (.D(RW), .en(l17), .Q(r17), .clk(c), .clr(r));
  Register #(.width(1), .trigger("falling")) register_8 (.D(RW), .en(l25), .Q(r25), .clk(c), .clr(r));
  Register #(.width(1), .trigger("falling")) register_9 (.D(RW), .en(l2), .Q(r2), .clk(c), .clr(r));
  Register #(.width(1), .trigger("falling")) register_10 (.D(RW), .en(l10), .Q(r10), .clk(c), .clr(r));
  Register #(.width(1), .trigger("falling")) register_11 (.D(RW), .en(l18), .Q(r18), .clk(c), .clr(r));
  Register #(.width(1), .trigger("falling")) register_12 (.D(RW), .en(l26), .Q(r26), .clk(c), .clr(r));
  Register #(.width(1), .trigger("falling")) register_13 (.D(RW), .en(l3), .Q(r3), .clk(c), .clr(r));
  Register #(.width(1), .trigger("falling")) register_14 (.D(RW), .en(l11), .Q(r11), .clk(c), .clr(r));
  Register #(.width(1), .trigger("falling")) register_15 (.D(RW), .en(l19), .Q(r19), .clk(c), .clr(r));
  Register #(.width(1), .trigger("falling")) register_16 (.D(RW), .en(l27), .Q(r27), .clk(c), .clr(r));
  Multiplexer #(.select(5), .enable("false")) multiplexer_1 (
    .in0(r0), .in1(r1), .in2(r2), .in3(r3), .in4(r4), .in5(r5), .in6(r6), .in7(r7), .in8(r8), .in9(r9),
    .in10(r10), .in11(r11), .in12(r12), .in13(r13), .in14(r14), .in15(r15), .in16(r16), .in17(r17),
    .in18(r18), .in19(r19), .in20(r20), .in21(r21), .in22(r22), .in23(r23), .in24(r24), .in25(r25),
    .in26(r26), .in27(r27), .in28(r28), .in29(r29), .in30(r30), .in31(r31), .out(OUTPUT), .sel(LS));
  Register #(.width(1), .trigger("falling")) register_17 (.D(RW), .en(l4), .Q(r4), .clk(c), .clr(r));
  Register #(.width(1), .trigger("falling")) register_18 (.D(RW), .en(l12), .Q(r12), .clk(c), .clr(r));
  Register #(.width(1), .trigger("falling")) register_19 (.D(RW), .en(l20), .Q(r20), .clk(c), .clr(r));
  Register #(.width(1), .trigger("falling")) register_20 (.D(RW), .en(l28), .Q(r28), .clk(c), .clr(r));
  Register #(.width(1), .trigger("falling")) register_21 (.D(RW), .en(l5), .Q(r5), .clk(c), .clr(r));
  Register #(.width(1), .trigger("falling")) register_22 (.D(RW), .en(l13), .Q(r13), .clk(c), .clr(r));
  Register #(.width(1), .trigger("falling")) register_23 (.D(RW), .en(l21), .Q(r21), .clk(c), .clr(r));
  Register #(.width(1), .trigger("falling")) register_24 (.D(RW), .en(l29), .Q(r29), .clk(c), .clr(r));
  Register #(.width(1), .trigger("falling")) register_25 (.D(RW), .en(l6), .Q(r6), .clk(c), .clr(r));
  Register #(.width(1), .trigger("falling")) register_26 (.D(RW), .en(l14), .Q(r14), .clk(c), .clr(r));
  Register #(.width(1), .trigger("falling")) register_27 (.D(RW), .en(l22), .Q(r22), .clk(c), .clr(r));
  Register #(.width(1), .trigger("falling")) register_28 (.D(RW), .en(l30), .Q(r30), .clk(c), .clr(r));
  Register #(.width(1), .trigger("falling")) register_29 (.D(RW), .en(l7), .Q(r7), .clk(c), .clr(r));
  Register #(.width(1), .trigger("falling")) register_30 (.D(RW), .en(l15), .Q(r15), .clk(c), .clr(r));
  Register #(.width(1), .trigger("falling")) register_31 (.D(RW), .en(l23), .Q(r23), .clk(c), .clr(r));
  Register #(.width(1), .trigger("falling")) register_32 (.D(RW), .en(l31), .Q(r31), .clk(c), .clr(r));

  // Other names for the same wires on the sheet: di = RW

  // Notes on the sheet:
  //   no afecta, pero tenia todos los valid en 1
  //   si es tristatico no modifica y si va a escribir se pone en 1 q es lo q quiero guardar, en los otros bancos entra ya tristate asi q 
  //   aca el input en 1 es lo ideal pues es lo q le entra, pero por el tristate del RW conviene cogerlo pq si no carga 1 en todos, 
endmodule

module selmask (
  input  [1:0] a,
  output [3:0] q
);

  wire not_1_out, not_2_out, not_3_out, not_4_out;

  and and_1 (q[3], a[1], a[0]);
  not not_1 (not_1_out, a[0]);
  not not_2 (not_2_out, a[1]);
  not not_3 (not_3_out, a[1]);
  not not_4 (not_4_out, a[0]);
  and and_2 (q[2], a[1], not_1_out);
  and and_3 (q[1], not_2_out, a[0]);
  and and_4 (q[0], not_3_out, not_4_out);
endmodule
